// Logisim project blg222_p1.circ as structural Verilog
module _8bit_register (
  input  CLOCK_SIGNAL,
  input  [7:0] INPUT,
  input  [1:0] FUNCSEL,
  input  ENABLER,
  output [7:0] OUTPUT
);

  wire [7:0] adder_1_out, adder_2_out, multiplexer_1_out;

  Hex_Digit_Display hex_digit_display_1 (.value(INPUT[7:4]));  // open: dp
  Hex_Digit_Display hex_digit_display_2 (.value(INPUT[3:0]));  // open: dp
  Hex_Digit_Display hex_digit_display_3 (.value(OUTPUT[7:4]));  // open: dp
  Hex_Digit_Display hex_digit_display_4 (.value(OUTPUT[3:0]));  // open: dp
  Adder adder_1 (.a(8'h1), .b(OUTPUT), .out(adder_1_out));  // open: cin, cout
  Adder adder_2 (.a(OUTPUT), .b({8{1'b1}}), .out(adder_2_out));  // open: cin, cout
  Multiplexer #(.select(2), .width(8), .enable("false")) multiplexer_1 (
    .in0({8{1'b0}}), .in1(INPUT), .in2(adder_1_out), .in3(adder_2_out), .out(multiplexer_1_out), .sel(FUNCSEL));
  D_Flip_Flop d_ff_1 (
    .clk(CLOCK_SIGNAL), .D(multiplexer_1_out[0]), .Q(OUTPUT[0]), .en(ENABLER));  // open: Qn, preset, reset
  D_Flip_Flop d_ff_2 (
    .clk(CLOCK_SIGNAL), .D(multiplexer_1_out[1]), .Q(OUTPUT[1]), .en(ENABLER));  // open: Qn, preset, reset
  D_Flip_Flop d_ff_3 (
    .clk(CLOCK_SIGNAL), .D(multiplexer_1_out[2]), .Q(OUTPUT[2]), .en(ENABLER));  // open: Qn, preset, reset
  D_Flip_Flop d_ff_4 (
    .clk(CLOCK_SIGNAL), .D(multiplexer_1_out[3]), .Q(OUTPUT[3]), .en(ENABLER));  // open: Qn, preset, reset
  D_Flip_Flop d_ff_5 (
    .clk(CLOCK_SIGNAL), .D(multiplexer_1_out[4]), .Q(OUTPUT[4]), .en(ENABLER));  // open: Qn, preset, reset
  D_Flip_Flop d_ff_6 (
    .clk(CLOCK_SIGNAL), .D(multiplexer_1_out[5]), .Q(OUTPUT[5]), .en(ENABLER));  // open: Qn, preset, reset
  D_Flip_Flop d_ff_7 (
    .clk(CLOCK_SIGNAL), .D(multiplexer_1_out[6]), .Q(OUTPUT[6]), .en(ENABLER));  // open: Qn, preset, reset
  D_Flip_Flop d_ff_8 (
    .clk(CLOCK_SIGNAL), .D(multiplexer_1_out[7]), .Q(OUTPUT[7]), .en(ENABLER));  // open: Qn, preset, reset

  // Notes on the sheet:
  //   INPUT DISPLAY
  //   OUTPUT DISPLAY
  //   clear
endmodule

module _16bit_register (
  input  CLOCK_SIGNAL,
  input  [15:0] INPUT,
  input  [1:0] FUNCSEL,
  input  ENABLER,
  output [15:0] OUTPUT
);

  wire [15:0] adder_1_out, adder_2_out, multiplexer_1_out;

  Hex_Digit_Display hex_digit_display_1 (.value(INPUT[15:12]));  // open: dp
  Hex_Digit_Display hex_digit_display_2 (.value(OUTPUT[15:12]));  // open: dp
  Hex_Digit_Display hex_digit_display_3 (.value(INPUT[7:4]));  // open: dp
  Hex_Digit_Display hex_digit_display_4 (.value(INPUT[11:8]));  // open: dp
  Hex_Digit_Display hex_digit_display_5 (.value(OUTPUT[11:8]));  // open: dp
  Hex_Digit_Display hex_digit_display_6 (.value(INPUT[3:0]));  // open: dp
  Hex_Digit_Display hex_digit_display_7 (.value(OUTPUT[3:0]));  // open: dp
  Hex_Digit_Display hex_digit_display_8 (.value(OUTPUT[7:4]));  // open: dp
  Adder #(.width(16)) adder_1 (.a(16'h1), .b(OUTPUT), .out(adder_1_out));  // open: cin, cout
  Adder #(.width(16)) adder_2 (.a(OUTPUT), .b({16{1'b1}}), .out(adder_2_out));  // open: cin, cout
  Multiplexer #(.select(2), .width(16), .enable("false")) multiplexer_1 (
    .in0({16{1'b0}}), .in1(INPUT), .in2(adder_1_out), .in3(adder_2_out), .out(multiplexer_1_out),
    .sel(FUNCSEL));
  D_Flip_Flop d_ff_1 (
    .clk(CLOCK_SIGNAL), .D(multiplexer_1_out[0]), .Q(OUTPUT[0]), .en(ENABLER));  // open: Qn, preset, reset
  D_Flip_Flop d_ff_2 (
    .clk(CLOCK_SIGNAL), .D(multiplexer_1_out[1]), .Q(OUTPUT[1]), .en(ENABLER));  // open: Qn, preset, reset
  D_Flip_Flop d_ff_3 (
    .clk(CLOCK_SIGNAL), .D(multiplexer_1_out[2]), .Q(OUTPUT[2]), .en(ENABLER));  // open: Qn, preset, reset
  D_Flip_Flop d_ff_4 (
    .clk(CLOCK_SIGNAL), .D(multiplexer_1_out[3]), .Q(OUTPUT[3]), .en(ENABLER));  // open: Qn, preset, reset
  D_Flip_Flop d_ff_5 (
    .clk(CLOCK_SIGNAL), .D(multiplexer_1_out[4]), .Q(OUTPUT[4]), .en(ENABLER));  // open: Qn, preset, reset
  D_Flip_Flop d_ff_6 (
    .clk(CLOCK_SIGNAL), .D(multiplexer_1_out[5]), .Q(OUTPUT[5]), .en(ENABLER));  // open: Qn, preset, reset
  D_Flip_Flop d_ff_7 (
    .clk(CLOCK_SIGNAL), .D(multiplexer_1_out[6]), .Q(OUTPUT[6]), .en(ENABLER));  // open: Qn, preset, reset
  D_Flip_Flop d_ff_8 (
    .clk(CLOCK_SIGNAL), .D(multiplexer_1_out[7]), .Q(OUTPUT[7]), .en(ENABLER));  // open: Qn, preset, reset
  D_Flip_Flop d_ff_9 (
    .clk(CLOCK_SIGNAL), .D(multiplexer_1_out[8]), .Q(OUTPUT[8]), .en(ENABLER));  // open: Qn, preset, reset
  D_Flip_Flop d_ff_10 (
    .clk(CLOCK_SIGNAL), .D(multiplexer_1_out[9]), .Q(OUTPUT[9]), .en(ENABLER));  // open: Qn, preset, reset
  D_Flip_Flop d_ff_11 (
    .clk(CLOCK_SIGNAL), .D(multiplexer_1_out[10]), .Q(OUTPUT[10]), .en(ENABLER));  // open: Qn, preset, reset
  D_Flip_Flop d_ff_12 (
    .clk(CLOCK_SIGNAL), .D(multiplexer_1_out[11]), .Q(OUTPUT[11]), .en(ENABLER));  // open: Qn, preset, reset
  D_Flip_Flop d_ff_13 (
    .clk(CLOCK_SIGNAL), .D(multiplexer_1_out[12]), .Q(OUTPUT[12]), .en(ENABLER));  // open: Qn, preset, reset
  D_Flip_Flop d_ff_14 (
    .clk(CLOCK_SIGNAL), .D(multiplexer_1_out[13]), .Q(OUTPUT[13]), .en(ENABLER));  // open: Qn, preset, reset
  D_Flip_Flop d_ff_15 (
    .clk(CLOCK_SIGNAL), .D(multiplexer_1_out[14]), .Q(OUTPUT[14]), .en(ENABLER));  // open: Qn, preset, reset
  D_Flip_Flop d_ff_16 (
    .clk(CLOCK_SIGNAL), .D(multiplexer_1_out[15]), .Q(OUTPUT[15]), .en(ENABLER));  // open: Qn, preset, reset

  // Notes on the sheet:
  //   INPUT DISPLAY
  //   OUTPUT DISPLAY
  //   clear
endmodule

module part2a (
  input  CLOCK,
  input  [7:0] INPUT,
  input  [1:0] FUNCSEL,
  input  [3:0] REGSEL,
  input  [1:0] O_P_SEL,
  input  [1:0] O_P_SEL_2,
  output [7:0] O_P_A,
  output [7:0] O_P_B
);

  wire [7:0] n8bit_register_1_output, n8bit_register_2_output, n8bit_register_3_output,
       n8bit_register_4_output;

  Hex_Digit_Display hex_digit_display_1 (.value(INPUT[7:4]));  // open: dp
  Hex_Digit_Display hex_digit_display_2 (.value(INPUT[3:0]));  // open: dp
  _8bit_register u_8bit_register_1 (
    .CLOCK_SIGNAL(CLOCK), .INPUT(INPUT), .FUNCSEL(FUNCSEL), .OUTPUT(n8bit_register_1_output),
    .ENABLER(REGSEL[0]));
  _8bit_register u_8bit_register_2 (
    .CLOCK_SIGNAL(CLOCK), .INPUT(INPUT), .FUNCSEL(FUNCSEL), .OUTPUT(n8bit_register_2_output),
    .ENABLER(REGSEL[1]));
  _8bit_register u_8bit_register_3 (
    .CLOCK_SIGNAL(CLOCK), .INPUT(INPUT), .FUNCSEL(FUNCSEL), .OUTPUT(n8bit_register_3_output),
    .ENABLER(REGSEL[2]));
  _8bit_register u_8bit_register_4 (
    .CLOCK_SIGNAL(CLOCK), .INPUT(INPUT), .FUNCSEL(FUNCSEL), .OUTPUT(n8bit_register_4_output),
    .ENABLER(REGSEL[3]));
  Multiplexer #(.select(2), .width(8), .enable("false")) multiplexer_1 (
    .in0(n8bit_register_1_output), .in1(n8bit_register_2_output), .in2(n8bit_register_3_output),
    .in3(n8bit_register_4_output), .out(O_P_A), .sel(O_P_SEL));
  Multiplexer #(.select(2), .width(8), .enable("false")) multiplexer_2 (
    .in0(n8bit_register_1_output), .in1(n8bit_register_2_output), .in2(n8bit_register_3_output),
    .in3(n8bit_register_4_output), .out(O_P_B), .sel(O_P_SEL_2));
  Hex_Digit_Display hex_digit_display_3 (.value(O_P_A[7:4]));  // open: dp
  Hex_Digit_Display hex_digit_display_4 (.value(O_P_B[7:4]));  // open: dp
  Hex_Digit_Display hex_digit_display_5 (.value(O_P_A[3:0]));  // open: dp
  Hex_Digit_Display hex_digit_display_6 (.value(O_P_B[3:0]));  // open: dp

  // Notes on the sheet:
  //   INPUT DISPLAY
  //   OUTPUT A DISPLAY
  //   OUTPUT B DISPLAY
endmodule

module part2b (
  input  CLOCK,
  input  [7:0] INPUT,
  input  [1:0] FUNCSEL,
  input  [2:0] REGSEL,
  input  [1:0] O_P_C_SEL,
  input  [1:0] O_P_D_SEL,
  output [7:0] OUTPUT_C,
  output [7:0] OUTPUT_D
);

  wire [7:0] AR_output, PC_output, SP_output;

  Hex_Digit_Display hex_digit_display_1 (.value(INPUT[3:0]));  // open: dp
  Hex_Digit_Display hex_digit_display_2 (.value(INPUT[7:4]));  // open: dp
  _8bit_register PC (.CLOCK_SIGNAL(CLOCK), .INPUT(INPUT), .FUNCSEL(FUNCSEL), .OUTPUT(PC_output), .ENABLER(REGSEL[0]));
  _8bit_register AR (.CLOCK_SIGNAL(CLOCK), .INPUT(INPUT), .FUNCSEL(FUNCSEL), .OUTPUT(AR_output), .ENABLER(REGSEL[1]));
  _8bit_register SP (.CLOCK_SIGNAL(CLOCK), .INPUT(INPUT), .FUNCSEL(FUNCSEL), .OUTPUT(SP_output), .ENABLER(REGSEL[2]));
  Hex_Digit_Display hex_digit_display_3 (.value(OUTPUT_C[7:4]));  // open: dp
  Multiplexer #(.select(2), .width(8), .enable("false")) multiplexer_1 (
    .in0(PC_output), .in1(AR_output), .in2(SP_output), .in3(PC_output), .out(OUTPUT_C), .sel(O_P_C_SEL));
  Multiplexer #(.select(2), .width(8), .enable("false")) multiplexer_2 (
    .in0(PC_output), .in1(AR_output), .in2(SP_output), .in3(PC_output), .out(OUTPUT_D), .sel(O_P_D_SEL));
  Hex_Digit_Display hex_digit_display_4 (.value(OUTPUT_C[3:0]));  // open: dp
  Hex_Digit_Display hex_digit_display_5 (.value(OUTPUT_D[7:4]));  // open: dp
  Hex_Digit_Display hex_digit_display_6 (.value(OUTPUT_D[3:0]));  // open: dp

  // Notes on the sheet:
  //   INPUT DISPLAY
  //   OUTPUT C DISPLAY
  //   OUTPUT D DISPLAY
endmodule

module part2c (
  input  CLOCK,
  input  [7:0] INPUT,
  input  L_H_SIGNAL,
  input  [1:0] FUNCSEL,
  input  ENABLE,
  output [15:0] out_6
);

  wire [15:0] adder_1_out, adder_2_out, multiplexer_1_out, multiplexer_2_out;

  Hex_Digit_Display hex_digit_display_1 (.value(out_6[15:12]));  // open: dp
  Hex_Digit_Display hex_digit_display_2 (.value(INPUT[7:4]));  // open: dp
  Hex_Digit_Display hex_digit_display_3 (.value(out_6[11:8]));  // open: dp
  Hex_Digit_Display hex_digit_display_4 (.value(out_6[7:4]));  // open: dp
  Hex_Digit_Display hex_digit_display_5 (.value(INPUT[3:0]));  // open: dp
  Hex_Digit_Display hex_digit_display_6 (.value(out_6[3:0]));  // open: dp
  Multiplexer #(.width(16), .enable("false")) multiplexer_1 (
    .in0({out_6[15:8], INPUT}), .in1({INPUT, out_6[7:0]}), .out(multiplexer_1_out), .sel(L_H_SIGNAL));
  Adder #(.width(16)) adder_1 (.a(out_6), .b({16{1'b1}}), .out(adder_1_out));  // open: cin, cout
  Adder #(.width(16)) adder_2 (.a(16'h1), .b(out_6), .out(adder_2_out));  // open: cin, cout
  Multiplexer #(.select(2), .width(16), .enable("false")) multiplexer_2 (
    .in0({16{1'b0}}), .in1(adder_2_out), .in2(adder_1_out), .in3(multiplexer_1_out), .out(multiplexer_2_out),
    .sel(FUNCSEL));
  D_Flip_Flop d_ff_1 (.clk(CLOCK), .D(multiplexer_2_out[0]), .Q(out_6[0]), .en(ENABLE));  // open: Qn, preset, reset
  D_Flip_Flop d_ff_2 (.clk(CLOCK), .D(multiplexer_2_out[1]), .Q(out_6[1]), .en(ENABLE));  // open: Qn, preset, reset
  D_Flip_Flop d_ff_3 (.clk(CLOCK), .D(multiplexer_2_out[2]), .Q(out_6[2]), .en(ENABLE));  // open: Qn, preset, reset
  D_Flip_Flop d_ff_4 (.clk(CLOCK), .D(multiplexer_2_out[3]), .Q(out_6[3]), .en(ENABLE));  // open: Qn, preset, reset
  D_Flip_Flop d_ff_5 (.clk(CLOCK), .D(multiplexer_2_out[4]), .Q(out_6[4]), .en(ENABLE));  // open: Qn, preset, reset
  D_Flip_Flop d_ff_6 (.clk(CLOCK), .D(multiplexer_2_out[5]), .Q(out_6[5]), .en(ENABLE));  // open: Qn, preset, reset
  D_Flip_Flop d_ff_7 (.clk(CLOCK), .D(multiplexer_2_out[6]), .Q(out_6[6]), .en(ENABLE));  // open: Qn, preset, reset
  D_Flip_Flop d_ff_8 (.clk(CLOCK), .D(multiplexer_2_out[7]), .Q(out_6[7]), .en(ENABLE));  // open: Qn, preset, reset
  D_Flip_Flop d_ff_9 (.clk(CLOCK), .D(multiplexer_2_out[8]), .Q(out_6[8]), .en(ENABLE));  // open: Qn, preset, reset
  D_Flip_Flop d_ff_10 (.clk(CLOCK), .D(multiplexer_2_out[9]), .Q(out_6[9]), .en(ENABLE));  // open: Qn, preset, reset
  D_Flip_Flop d_ff_11 (.clk(CLOCK), .D(multiplexer_2_out[10]), .Q(out_6[10]), .en(ENABLE));  // open: Qn, preset, reset
  D_Flip_Flop d_ff_12 (.clk(CLOCK), .D(multiplexer_2_out[11]), .Q(out_6[11]), .en(ENABLE));  // open: Qn, preset, reset
  D_Flip_Flop d_ff_13 (.clk(CLOCK), .D(multiplexer_2_out[12]), .Q(out_6[12]), .en(ENABLE));  // open: Qn, preset, reset
  D_Flip_Flop d_ff_14 (.clk(CLOCK), .D(multiplexer_2_out[13]), .Q(out_6[13]), .en(ENABLE));  // open: Qn, preset, reset
  D_Flip_Flop d_ff_15 (.clk(CLOCK), .D(multiplexer_2_out[14]), .Q(out_6[14]), .en(ENABLE));  // open: Qn, preset, reset
  D_Flip_Flop d_ff_16 (.clk(CLOCK), .D(multiplexer_2_out[15]), .Q(out_6[15]), .en(ENABLE));  // open: Qn, preset, reset

  // Notes on the sheet:
  //   INPUT DISPLAY
  //   OUTPUT DISPLAY
endmodule
