// Logisim project blg222_p2.circ as structural Verilog
module _8bit_register (
  input  CLOCK_SIGNAL,
  input  [7:0] INPUT,
  input  [1:0] FunSel,
  input  ENABLER,
  output [7:0] OUTPUT
);

  wire [7:0] adder_1_out, bit_extender_1_out, multiplexer_1_out, xor_1_out;

  Hex_Digit_Display hex_digit_display_1 (.value(INPUT[7:4]));  // open: dp
  Hex_Digit_Display hex_digit_display_2 (.value(INPUT[3:0]));  // open: dp
  Hex_Digit_Display hex_digit_display_3 (.value(OUTPUT[7:4]));  // open: dp
  Hex_Digit_Display hex_digit_display_4 (.value(OUTPUT[3:0]));  // open: dp
  assign xor_1_out = 8'h1 ^ bit_extender_1_out;  // XOR_Gate xor_1, 8 bits wide
  assign bit_extender_1_out = {{7{FunSel[0]}}, FunSel[0]};  // Bit_Extender bit_extender_1
  Adder adder_1 (.a(xor_1_out), .b(OUTPUT), .out(adder_1_out), .cin(FunSel[0]));  // open: cout
  Multiplexer #(.select(2), .width(8), .enable("false")) multiplexer_1 (
    .in0({8{1'b0}}), .in1(INPUT), .in2(adder_1_out), .in3(adder_1_out), .out(multiplexer_1_out), .sel(FunSel));
  D_Flip_Flop d_ff_1 (
    .clk(CLOCK_SIGNAL), .D(multiplexer_1_out[0]), .Q(OUTPUT[0]), .en(ENABLER));  // open: Qn, preset, reset
  D_Flip_Flop d_ff_2 (
    .clk(CLOCK_SIGNAL), .D(multiplexer_1_out[1]), .Q(OUTPUT[1]), .en(ENABLER));  // open: Qn, preset, reset
  D_Flip_Flop d_ff_3 (
    .clk(CLOCK_SIGNAL), .D(multiplexer_1_out[2]), .Q(OUTPUT[2]), .en(ENABLER));  // open: Qn, preset, reset
  D_Flip_Flop d_ff_4 (
    .clk(CLOCK_SIGNAL), .D(multiplexer_1_out[3]), .Q(OUTPUT[3]), .en(ENABLER));  // open: Qn, preset, reset
  D_Flip_Flop d_ff_5 (
    .clk(CLOCK_SIGNAL), .D(multiplexer_1_out[4]), .Q(OUTPUT[4]), .en(ENABLER));  // open: Qn, preset, reset
  D_Flip_Flop d_ff_6 (
    .clk(CLOCK_SIGNAL), .D(multiplexer_1_out[5]), .Q(OUTPUT[5]), .en(ENABLER));  // open: Qn, preset, reset
  D_Flip_Flop d_ff_7 (
    .clk(CLOCK_SIGNAL), .D(multiplexer_1_out[6]), .Q(OUTPUT[6]), .en(ENABLER));  // open: Qn, preset, reset
  D_Flip_Flop d_ff_8 (
    .clk(CLOCK_SIGNAL), .D(multiplexer_1_out[7]), .Q(OUTPUT[7]), .en(ENABLER));  // open: Qn, preset, reset

  // Notes on the sheet:
  //   INPUT DISPLAY
  //   OUTPUT DISPLAY
  //   clear
endmodule

module _16bit_register (
  input  CLOCK_SIGNAL,
  input  [15:0] INPUT,
  input  [1:0] FunSel,
  input  ENABLER,
  output [15:0] OUTPUT
);

  wire [15:0] adder_1_out, bit_extender_1_out, multiplexer_1_out, xor_1_out;

  Hex_Digit_Display hex_digit_display_1 (.value(INPUT[15:12]));  // open: dp
  Hex_Digit_Display hex_digit_display_2 (.value(OUTPUT[15:12]));  // open: dp
  Hex_Digit_Display hex_digit_display_3 (.value(INPUT[11:8]));  // open: dp
  Hex_Digit_Display hex_digit_display_4 (.value(INPUT[7:4]));  // open: dp
  Hex_Digit_Display hex_digit_display_5 (.value(OUTPUT[11:8]));  // open: dp
  Hex_Digit_Display hex_digit_display_6 (.value(INPUT[3:0]));  // open: dp
  Hex_Digit_Display hex_digit_display_7 (.value(OUTPUT[7:4]));  // open: dp
  Hex_Digit_Display hex_digit_display_8 (.value(OUTPUT[3:0]));  // open: dp
  assign bit_extender_1_out = {{15{FunSel[0]}}, FunSel[0]};  // Bit_Extender bit_extender_1
  assign xor_1_out = 16'h1 ^ bit_extender_1_out;  // XOR_Gate xor_1, 16 bits wide
  Adder #(.width(16)) adder_1 (.a(xor_1_out), .b(OUTPUT), .out(adder_1_out), .cin(FunSel[0]));  // open: cout
  Multiplexer #(.select(2), .width(16), .enable("false")) multiplexer_1 (
    .in0({16{1'b0}}), .in1(INPUT), .in2(adder_1_out), .in3(adder_1_out), .out(multiplexer_1_out), .sel(FunSel));
  D_Flip_Flop d_ff_1 (
    .clk(CLOCK_SIGNAL), .D(multiplexer_1_out[0]), .Q(OUTPUT[0]), .en(ENABLER));  // open: Qn, preset, reset
  D_Flip_Flop d_ff_2 (
    .clk(CLOCK_SIGNAL), .D(multiplexer_1_out[1]), .Q(OUTPUT[1]), .en(ENABLER));  // open: Qn, preset, reset
  D_Flip_Flop d_ff_3 (
    .clk(CLOCK_SIGNAL), .D(multiplexer_1_out[2]), .Q(OUTPUT[2]), .en(ENABLER));  // open: Qn, preset, reset
  D_Flip_Flop d_ff_4 (
    .clk(CLOCK_SIGNAL), .D(multiplexer_1_out[3]), .Q(OUTPUT[3]), .en(ENABLER));  // open: Qn, preset, reset
  D_Flip_Flop d_ff_5 (
    .clk(CLOCK_SIGNAL), .D(multiplexer_1_out[4]), .Q(OUTPUT[4]), .en(ENABLER));  // open: Qn, preset, reset
  D_Flip_Flop d_ff_6 (
    .clk(CLOCK_SIGNAL), .D(multiplexer_1_out[5]), .Q(OUTPUT[5]), .en(ENABLER));  // open: Qn, preset, reset
  D_Flip_Flop d_ff_7 (
    .clk(CLOCK_SIGNAL), .D(multiplexer_1_out[6]), .Q(OUTPUT[6]), .en(ENABLER));  // open: Qn, preset, reset
  D_Flip_Flop d_ff_8 (
    .clk(CLOCK_SIGNAL), .D(multiplexer_1_out[7]), .Q(OUTPUT[7]), .en(ENABLER));  // open: Qn, preset, reset
  D_Flip_Flop d_ff_9 (
    .clk(CLOCK_SIGNAL), .D(multiplexer_1_out[8]), .Q(OUTPUT[8]), .en(ENABLER));  // open: Qn, preset, reset
  D_Flip_Flop d_ff_10 (
    .clk(CLOCK_SIGNAL), .D(multiplexer_1_out[9]), .Q(OUTPUT[9]), .en(ENABLER));  // open: Qn, preset, reset
  D_Flip_Flop d_ff_11 (
    .clk(CLOCK_SIGNAL), .D(multiplexer_1_out[10]), .Q(OUTPUT[10]), .en(ENABLER));  // open: Qn, preset, reset
  D_Flip_Flop d_ff_12 (
    .clk(CLOCK_SIGNAL), .D(multiplexer_1_out[11]), .Q(OUTPUT[11]), .en(ENABLER));  // open: Qn, preset, reset
  D_Flip_Flop d_ff_13 (
    .clk(CLOCK_SIGNAL), .D(multiplexer_1_out[12]), .Q(OUTPUT[12]), .en(ENABLER));  // open: Qn, preset, reset
  D_Flip_Flop d_ff_14 (
    .clk(CLOCK_SIGNAL), .D(multiplexer_1_out[13]), .Q(OUTPUT[13]), .en(ENABLER));  // open: Qn, preset, reset
  D_Flip_Flop d_ff_15 (
    .clk(CLOCK_SIGNAL), .D(multiplexer_1_out[14]), .Q(OUTPUT[14]), .en(ENABLER));  // open: Qn, preset, reset
  D_Flip_Flop d_ff_16 (
    .clk(CLOCK_SIGNAL), .D(multiplexer_1_out[15]), .Q(OUTPUT[15]), .en(ENABLER));  // open: Qn, preset, reset

  // Notes on the sheet:
  //   INPUT DISPLAY
  //   OUTPUT DISPLAY
  //   clear
endmodule

module part2a (
  input  CLOCK,
  input  [7:0] INPUT,
  input  [1:0] FUNSEL,
  input  [3:0] REGSEL,
  input  [1:0] OutASel,
  input  [1:0] OutBSel,
  output [7:0] OutA,
  output [7:0] OutB
);

  wire [7:0] n8bit_register_1_output, n8bit_register_2_output, n8bit_register_3_output,
       n8bit_register_4_output;

  Hex_Digit_Display hex_digit_display_1 (.value(INPUT[7:4]));  // open: dp
  Hex_Digit_Display hex_digit_display_2 (.value(INPUT[3:0]));  // open: dp
  _8bit_register u_8bit_register_1 (
    .CLOCK_SIGNAL(CLOCK), .INPUT(INPUT), .FunSel(FUNSEL), .OUTPUT(n8bit_register_1_output),
    .ENABLER(REGSEL[0]));
  _8bit_register u_8bit_register_2 (
    .CLOCK_SIGNAL(CLOCK), .INPUT(INPUT), .FunSel(FUNSEL), .OUTPUT(n8bit_register_2_output),
    .ENABLER(REGSEL[1]));
  _8bit_register u_8bit_register_3 (
    .CLOCK_SIGNAL(CLOCK), .INPUT(INPUT), .FunSel(FUNSEL), .OUTPUT(n8bit_register_3_output),
    .ENABLER(REGSEL[2]));
  _8bit_register u_8bit_register_4 (
    .CLOCK_SIGNAL(CLOCK), .INPUT(INPUT), .FunSel(FUNSEL), .OUTPUT(n8bit_register_4_output),
    .ENABLER(REGSEL[3]));
  Multiplexer #(.select(2), .width(8), .enable("false")) multiplexer_1 (
    .in0(n8bit_register_1_output), .in1(n8bit_register_2_output), .in2(n8bit_register_3_output),
    .in3(n8bit_register_4_output), .out(OutA), .sel(OutASel));
  Multiplexer #(.select(2), .width(8), .enable("false")) multiplexer_2 (
    .in0(n8bit_register_1_output), .in1(n8bit_register_2_output), .in2(n8bit_register_3_output),
    .in3(n8bit_register_4_output), .out(OutB), .sel(OutBSel));
  Hex_Digit_Display hex_digit_display_3 (.value(OutA[7:4]));  // open: dp
  Hex_Digit_Display hex_digit_display_4 (.value(OutB[7:4]));  // open: dp
  Hex_Digit_Display hex_digit_display_5 (.value(OutA[3:0]));  // open: dp
  Hex_Digit_Display hex_digit_display_6 (.value(OutB[3:0]));  // open: dp

  // Notes on the sheet:
  //   INPUT DISPLAY
  //   OUTPUT A DISPLAY
  //   OUTPUT B DISPLAY
endmodule

module part2b (
  input  CLOCK,
  input  [7:0] INPUT,
  input  [1:0] FunSel,
  input  [2:0] RegSel,
  input  [1:0] OutCSel,
  input  [1:0] OutDSel,
  output [7:0] OUTPUT_C,
  output [7:0] OUTPUT_D
);

  wire [7:0] AR_output, PC_output, SP_output;

  Hex_Digit_Display hex_digit_display_1 (.value(INPUT[7:4]));  // open: dp
  Hex_Digit_Display hex_digit_display_2 (.value(INPUT[3:0]));  // open: dp
  _8bit_register PC (.CLOCK_SIGNAL(CLOCK), .INPUT(INPUT), .FunSel(FunSel), .OUTPUT(PC_output), .ENABLER(RegSel[0]));
  _8bit_register AR (.CLOCK_SIGNAL(CLOCK), .INPUT(INPUT), .FunSel(FunSel), .OUTPUT(AR_output), .ENABLER(RegSel[1]));
  _8bit_register SP (.CLOCK_SIGNAL(CLOCK), .INPUT(INPUT), .FunSel(FunSel), .OUTPUT(SP_output), .ENABLER(RegSel[2]));
  Hex_Digit_Display hex_digit_display_3 (.value(OUTPUT_C[7:4]));  // open: dp
  Multiplexer #(.select(2), .width(8), .enable("false")) multiplexer_1 (
    .in0(PC_output), .in1(AR_output), .in2(SP_output), .in3(PC_output), .out(OUTPUT_C), .sel(OutCSel));
  Multiplexer #(.select(2), .width(8), .enable("false")) multiplexer_2 (
    .in0(PC_output), .in1(AR_output), .in2(SP_output), .in3(PC_output), .out(OUTPUT_D), .sel(OutDSel));
  Hex_Digit_Display hex_digit_display_4 (.value(OUTPUT_C[3:0]));  // open: dp
  Hex_Digit_Display hex_digit_display_5 (.value(OUTPUT_D[7:4]));  // open: dp
  Hex_Digit_Display hex_digit_display_6 (.value(OUTPUT_D[3:0]));  // open: dp

  // Notes on the sheet:
  //   INPUT DISPLAY
  //   OUTPUT C DISPLAY
  //   OUTPUT D DISPLAY
endmodule

module part2c (
  input  CLOCK,
  input  [7:0] INPUT,
  input  L_H_SIGNAL,
  input  [1:0] FunSel,
  input  ENABLE,
  output [7:0] Out_High,
  output [7:0] Out_Low
);

  wire [15:0] adder_1_out, bit_extender_1_out, multiplexer_1_out, multiplexer_2_out, xor_1_out;

  Hex_Digit_Display hex_digit_display_1 (.value(Out_High[7:4]));  // open: dp
  Hex_Digit_Display hex_digit_display_2 (.value(INPUT[7:4]));  // open: dp
  Hex_Digit_Display hex_digit_display_3 (.value(Out_Low[7:4]));  // open: dp
  Hex_Digit_Display hex_digit_display_4 (.value(Out_High[3:0]));  // open: dp
  Hex_Digit_Display hex_digit_display_5 (.value(INPUT[3:0]));  // open: dp
  Hex_Digit_Display hex_digit_display_6 (.value(Out_Low[3:0]));  // open: dp
  Multiplexer #(.width(16), .enable("false")) multiplexer_1 (
    .in0({Out_High, INPUT}), .in1({INPUT, Out_Low}), .out(multiplexer_1_out), .sel(L_H_SIGNAL));
  assign xor_1_out = 16'h1 ^ bit_extender_1_out;  // XOR_Gate xor_1, 16 bits wide
  assign bit_extender_1_out = {{15{FunSel[1]}}, FunSel[1]};  // Bit_Extender bit_extender_1
  Adder #(.width(16)) adder_1 (
    .a(xor_1_out), .b({Out_High, Out_Low}), .out(adder_1_out), .cin(FunSel[1]));  // open: cout
  Multiplexer #(.select(2), .width(16), .enable("false")) multiplexer_2 (
    .in0({16{1'b0}}), .in1(adder_1_out), .in2(adder_1_out), .in3(multiplexer_1_out), .out(multiplexer_2_out),
    .sel(FunSel));
  D_Flip_Flop d_ff_1 (.clk(CLOCK), .D(multiplexer_2_out[0]), .Q(Out_Low[0]), .en(ENABLE));  // open: Qn, preset, reset
  D_Flip_Flop d_ff_2 (.clk(CLOCK), .D(multiplexer_2_out[1]), .Q(Out_Low[1]), .en(ENABLE));  // open: Qn, preset, reset
  D_Flip_Flop d_ff_3 (.clk(CLOCK), .D(multiplexer_2_out[2]), .Q(Out_Low[2]), .en(ENABLE));  // open: Qn, preset, reset
  D_Flip_Flop d_ff_4 (.clk(CLOCK), .D(multiplexer_2_out[3]), .Q(Out_Low[3]), .en(ENABLE));  // open: Qn, preset, reset
  D_Flip_Flop d_ff_5 (.clk(CLOCK), .D(multiplexer_2_out[4]), .Q(Out_Low[4]), .en(ENABLE));  // open: Qn, preset, reset
  D_Flip_Flop d_ff_6 (.clk(CLOCK), .D(multiplexer_2_out[5]), .Q(Out_Low[5]), .en(ENABLE));  // open: Qn, preset, reset
  D_Flip_Flop d_ff_7 (.clk(CLOCK), .D(multiplexer_2_out[6]), .Q(Out_Low[6]), .en(ENABLE));  // open: Qn, preset, reset
  D_Flip_Flop d_ff_8 (.clk(CLOCK), .D(multiplexer_2_out[7]), .Q(Out_Low[7]), .en(ENABLE));  // open: Qn, preset, reset
  D_Flip_Flop d_ff_9 (.clk(CLOCK), .D(multiplexer_2_out[8]), .Q(Out_High[0]), .en(ENABLE));  // open: Qn, preset, reset
  D_Flip_Flop d_ff_10 (.clk(CLOCK), .D(multiplexer_2_out[9]), .Q(Out_High[1]), .en(ENABLE));  // open: Qn, preset, reset
  D_Flip_Flop d_ff_11 (
    .clk(CLOCK), .D(multiplexer_2_out[10]), .Q(Out_High[2]), .en(ENABLE));  // open: Qn, preset, reset
  D_Flip_Flop d_ff_12 (
    .clk(CLOCK), .D(multiplexer_2_out[11]), .Q(Out_High[3]), .en(ENABLE));  // open: Qn, preset, reset
  D_Flip_Flop d_ff_13 (
    .clk(CLOCK), .D(multiplexer_2_out[12]), .Q(Out_High[4]), .en(ENABLE));  // open: Qn, preset, reset
  D_Flip_Flop d_ff_14 (
    .clk(CLOCK), .D(multiplexer_2_out[13]), .Q(Out_High[5]), .en(ENABLE));  // open: Qn, preset, reset
  D_Flip_Flop d_ff_15 (
    .clk(CLOCK), .D(multiplexer_2_out[14]), .Q(Out_High[6]), .en(ENABLE));  // open: Qn, preset, reset
  D_Flip_Flop d_ff_16 (
    .clk(CLOCK), .D(multiplexer_2_out[15]), .Q(Out_High[7]), .en(ENABLE));  // open: Qn, preset, reset

  // Notes on the sheet:
  //   INPUT DISPLAY
  //   OUTPUT DISPLAY
endmodule

module ALU (
  input  CLOCK,
  input  [7:0] A,
  input  [7:0] B,
  input  [3:0] FUNSEL,
  output [3:0] ZCNO,
  output [7:0] OutFLAG
);

  wire adder_1_cout, adder_2_cout, and_1_out, and_3_out, multiplexer_1_out, multiplexer_3_out,
       multiplexer_5_out, nor_1_out, not_3_out, or_1_out, xor_2_out, xor_3_out, xor_5_out;
  wire [0:0] multiplexer_2_out;
  wire [6:0] adder_1_out;
  wire [7:0] and_2_out, bit_extender_1_out, not_1_out, not_2_out, or_2_out, xor_1_out, xor_4_out;
  wire [7:7] adder_2_out, multiplexer_4_out;

  Multiplexer #(.select(4), .enable("false")) multiplexer_1 (
    .in0(ZCNO[0]), .in1(ZCNO[0]), .in2(ZCNO[0]), .in3(ZCNO[0]), .in4(xor_3_out), .in5(xor_3_out),
    .in6(xor_3_out), .in7(ZCNO[0]), .in8(ZCNO[0]), .in9(ZCNO[0]), .in10(ZCNO[0]), .in11(ZCNO[0]),
    .in12(xor_2_out), .in13(ZCNO[0]), .in14(xor_2_out), .in15(xor_5_out), .out(multiplexer_1_out),
    .sel(FUNSEL));
  assign bit_extender_1_out = {{7{FUNSEL[1]}}, FUNSEL[1]};  // Bit_Extender bit_extender_1
  D_Flip_Flop O (.clk(CLOCK), .D(multiplexer_1_out), .Q(ZCNO[0]));  // open: Qn, preset, en, reset
  assign xor_1_out = B ^ bit_extender_1_out;  // XOR_Gate xor_1, 8 bits wide
  assign not_1_out = ~A;  // NOT_Gate not_1, 8 bits wide
  assign not_2_out = ~B;  // NOT_Gate not_2, 8 bits wide
  Multiplexer #(.select(2), .enable("false")) multiplexer_2 (
    .in1(1'b0), .in2(1'b0), .in3(ZCNO[2]), .out(multiplexer_2_out[0]), .sel(FUNSEL[2:1]));  // open: in0
  and and_1 (and_1_out, ZCNO[2], FUNSEL[0]);
  xor xor_2 (xor_2_out, A[7], A[6]);
  Hex_Digit_Display hex_digit_display_1 (.value(A[7:4]));  // open: dp
  Multiplexer #(.select(4), .enable("false")) multiplexer_3 (
    .in0(ZCNO[2]), .in1(ZCNO[2]), .in2(ZCNO[2]), .in3(ZCNO[2]), .in4(adder_2_cout), .in5(adder_2_cout),
    .in6(adder_2_cout), .in7(ZCNO[2]), .in8(ZCNO[2]), .in9(ZCNO[2]), .in10(A[7]), .in11(A[0]),
    .in12(ZCNO[2]), .in13(ZCNO[2]), .in14(A[7]), .in15(A[0]), .out(multiplexer_3_out), .sel(FUNSEL));
  or or_1 (or_1_out, and_1_out, FUNSEL[1]);
  Hex_Digit_Display hex_digit_display_2 (.value(A[3:0]));  // open: dp
  D_Flip_Flop C (.clk(CLOCK), .D(multiplexer_3_out), .Q(ZCNO[2]));  // open: Qn, preset, en, reset
  Adder #(.width(7)) adder_1 (.a(A[6:0]), .b(xor_1_out[6:0]), .out(adder_1_out), .cin(or_1_out), .cout(adder_1_cout));
  Adder #(.width(1)) adder_2 (
    .a(A[7]), .b(xor_1_out[7]), .out(adder_2_out[7]), .cin(adder_1_cout), .cout(adder_2_cout));
  assign and_2_out = A & B;  // AND_Gate and_2, 8 bits wide
  Hex_Digit_Display hex_digit_display_3 (.value(B[7:4]));  // open: dp
  xor xor_3 (xor_3_out, adder_1_cout, adder_2_cout);
  assign or_2_out = A | B;  // OR_Gate or_2, 8 bits wide
  assign xor_4_out = A ^ B;  // XOR_Gate xor_4, 8 bits wide
  Multiplexer #(.select(2), .enable("false")) multiplexer_4 (
    .in0(1'b1), .in1(1'b0), .in2(A[7]), .in3(ZCNO[2]), .out(multiplexer_4_out[7]), .sel(FUNSEL[2:1]));
  Hex_Digit_Display hex_digit_display_4 (.value(B[3:0]));  // open: dp
  nor nor_1 (nor_1_out, OutFLAG[0], OutFLAG[1], OutFLAG[2], OutFLAG[3], OutFLAG[4], OutFLAG[5], OutFLAG[6], OutFLAG[7]);
  D_Flip_Flop Z (.clk(CLOCK), .D(nor_1_out), .Q(ZCNO[3]));  // open: Qn, preset, en, reset
  xor xor_5 (xor_5_out, A[7], multiplexer_4_out[7]);
  Hex_Digit_Display hex_digit_display_5 (.value(FUNSEL));  // open: dp
  Multiplexer #(.enable("false")) multiplexer_5 (
    .in0(OutFLAG[7]), .in1(ZCNO[1]), .out(multiplexer_5_out), .sel(and_3_out));
  and and_3 (and_3_out, FUNSEL[0], not_3_out, FUNSEL[2], FUNSEL[3]);
  D_Flip_Flop N (.clk(CLOCK), .D(multiplexer_5_out), .Q(ZCNO[1]));  // open: Qn, preset, en, reset
  not not_3 (not_3_out, FUNSEL[1]);
  Multiplexer #(.select(4), .width(8), .enable("false")) multiplexer_6 (
    .in0(A), .in1(B), .in2(not_1_out), .in3(not_2_out), .in4({adder_2_out[7], adder_1_out}),
    .in5({adder_2_out[7], adder_1_out}), .in6({adder_2_out[7], adder_1_out}), .in7(and_2_out),
    .in8(or_2_out), .in9(xor_4_out), .in10({A[6:0], multiplexer_2_out[0]}),
    .in11({multiplexer_4_out[7], A[7:1]}), .in12({A[6:0], multiplexer_2_out[0]}),
    .in13({multiplexer_4_out[7], A[7:1]}), .in14({A[6:0], multiplexer_2_out[0]}),
    .in15({multiplexer_4_out[7], A[7:1]}), .out(OutFLAG), .sel(FUNSEL));
  Hex_Digit_Display hex_digit_display_6 (.value(OutFLAG[7:4]));  // open: dp
  Hex_Digit_Display hex_digit_display_7 (.value(ZCNO));  // open: dp
  Hex_Digit_Display hex_digit_display_8 (.value(OutFLAG[3:0]));  // open: dp

  // Notes on the sheet:
  //   A
  //   B
  //   FUNSEL
  //   OutFlag
  //   ZCNO
endmodule

module \new  (
  input  CLOCK,
  input  [3:0] FUNSEL_ALU,
  input  [1:0] OutASel,
  input  [1:0] OutBSel,
  input  [1:0] FunSel,
  input  [3:0] RegSel,
  input  Store,
  input  Load,
  input  L_H,
  input  [1:0] funseL_2,
  input  Enable,
  input  [1:0] OutCSel,
  input  [1:0] MuxASEL,
  input  [1:0] MuxBSel,
  input  [1:0] OutDSel,
  input  [1:0] FunSel_3,
  input  MuxCSEL,
  input  [2:0] RegSel_2,
  output [7:0] IR_8_15
);

  wire [3:0] ALU_outflag, ALU_zcno, multiplexer_2_out, multiplexer_2_out_2, part2c_1_out_low,
       part2c_1_out_low_2, ram_1_data, ram_1_data_2;
  wire [7:0] multiplexer_1_out, multiplexer_3_out, P1_Part2a_outa, P1_Part2a_outb, P1_Part2b_output_c,
       P1_Part2b_output_d;
  wire [7:4] ALU_outflag_2;

  Hex_Digit_Display hex_digit_display_1 (.value(multiplexer_1_out[7:4]));  // open: dp
  Multiplexer #(.select(2), .width(8), .enable("false")) multiplexer_1 (
    .in0({part2c_1_out_low_2, part2c_1_out_low}), .in1({ram_1_data_2, ram_1_data}), .in2(P1_Part2b_output_c),
    .in3({ALU_outflag_2, ALU_outflag}), .out(multiplexer_1_out), .sel(MuxASEL));
  Hex_Digit_Display hex_digit_display_2 (.value(part2c_1_out_low_2));  // open: dp
  Hex_Digit_Display hex_digit_display_3 (.value(part2c_1_out_low));  // open: dp
  Hex_Digit_Display hex_digit_display_4 (.value(multiplexer_1_out[3:0]));  // open: dp
  part2a P1_Part2a (
    .CLOCK(CLOCK), .OutA(P1_Part2a_outa), .INPUT(multiplexer_1_out), .FUNSEL(FunSel), .OutB(P1_Part2a_outb),
    .REGSEL(RegSel), .OutASel(OutASel), .OutBSel(OutBSel));
  part2c part2c_1 (
    .Out_High(IR_8_15), .CLOCK(CLOCK), .Out_Low({part2c_1_out_low_2, part2c_1_out_low}),
    .INPUT({ram_1_data_2, ram_1_data}), .L_H_SIGNAL(L_H), .FunSel(funseL_2), .ENABLE(Enable));
  Multiplexer #(.width(8), .enable("false")) multiplexer_2 (
    .in0(multiplexer_1_out), .in1(P1_Part2a_outa), .out({multiplexer_2_out_2, multiplexer_2_out}),
    .sel(MuxCSEL));
  Multiplexer #(.select(2), .width(8), .enable("false")) multiplexer_3 (
    .in0({part2c_1_out_low_2, part2c_1_out_low}), .in1({part2c_1_out_low_2, part2c_1_out_low}),
    .in2({ram_1_data_2, ram_1_data}), .in3({ALU_outflag_2, ALU_outflag}), .out(multiplexer_3_out),
    .sel(MuxBSel));
  Hex_Digit_Display hex_digit_display_5 (.value(multiplexer_2_out_2));  // open: dp
  Hex_Digit_Display hex_digit_display_6 (.value(multiplexer_2_out));  // open: dp
  part2b P1_Part2b (
    .CLOCK(CLOCK), .INPUT(multiplexer_3_out), .FunSel(FunSel_3), .RegSel(RegSel_2), .OutCSel(OutCSel),
    .OutDSel(OutDSel), .OUTPUT_C(P1_Part2b_output_c), .OUTPUT_D(P1_Part2b_output_d));
  Hex_Digit_Display hex_digit_display_7 (.value(ALU_zcno));  // open: dp
  ALU ALU (
    .CLOCK(CLOCK), .A({multiplexer_2_out_2, multiplexer_2_out}), .B(P1_Part2a_outb), .FUNSEL(FUNSEL_ALU),
    .ZCNO(ALU_zcno), .OutFLAG({ALU_outflag_2, ALU_outflag}));
  Hex_Digit_Display hex_digit_display_8 (.value(ALU_outflag_2));  // open: dp
  Hex_Digit_Display hex_digit_display_9 (.value(P1_Part2b_output_d[7:4]));  // open: dp
  Hex_Digit_Display hex_digit_display_10 (.value(ALU_outflag));  // open: dp
  Hex_Digit_Display hex_digit_display_11 (.value(P1_Part2b_output_d[3:0]));  // open: dp
  Hex_Digit_Display hex_digit_display_12 (.value(ram_1_data_2));  // open: dp
  Hex_Digit_Display hex_digit_display_13 (.value(ram_1_data));  // open: dp
  RAM #(.bus("separate")) ram_1 (
    .addr(P1_Part2b_output_d), .din({ALU_outflag_2, ALU_outflag}), .data({ram_1_data_2, ram_1_data}),
    .str(Store), .clk(CLOCK), .ld(Load));  // open: sel, clr
  Hex_Digit_Display hex_digit_display_14 (.value(IR_8_15[3:0]));  // open: dp
  Hex_Digit_Display hex_digit_display_15 (.value(IR_8_15[7:4]));  // open: dp

  // Notes on the sheet:
  //   OUTPUT DISPLAY
  //   OUTPUT DISPLAY
  //   MUX A
  //   MUX C
  //   MUX B
  //   ALU INPUT A
  //   ZCNO
  //   OUTPUT DISPLAY
  //   OUTPUT ALU
  //   OUTPUT DISPLAY
endmodule
