// Logisim project blg222_p3.circ as structural Verilog
module _8bit_register (
  input  CLOCK_SIGNAL,
  input  [7:0] INPUT,
  input  [1:0] FunSel,
  input  ENABLER,
  output [7:0] OUTPUT
);

  wire [7:0] adder_1_out, bit_extender_1_out, multiplexer_1_out, xor_1_out;

  Hex_Digit_Display hex_digit_display_1 (.value(INPUT[7:4]));  // open: dp
  Hex_Digit_Display hex_digit_display_2 (.value(INPUT[3:0]));  // open: dp
  Hex_Digit_Display hex_digit_display_3 (.value(OUTPUT[7:4]));  // open: dp
  Hex_Digit_Display hex_digit_display_4 (.value(OUTPUT[3:0]));  // open: dp
  assign xor_1_out = 8'h1 ^ bit_extender_1_out;  // XOR_Gate xor_1, 8 bits wide
  assign bit_extender_1_out = {{7{FunSel[0]}}, FunSel[0]};  // Bit_Extender bit_extender_1
  Adder adder_1 (.a(xor_1_out), .b(OUTPUT), .out(adder_1_out), .cin(FunSel[0]));  // open: cout
  Multiplexer #(.select(2), .width(8), .enable("false")) multiplexer_1 (
    .in0({8{1'b0}}), .in1(INPUT), .in2(adder_1_out), .in3(adder_1_out), .out(multiplexer_1_out), .sel(FunSel));
  D_Flip_Flop d_ff_1 (
    .clk(CLOCK_SIGNAL), .D(multiplexer_1_out[0]), .Q(OUTPUT[0]), .en(ENABLER));  // open: Qn, preset, reset
  D_Flip_Flop d_ff_2 (
    .clk(CLOCK_SIGNAL), .D(multiplexer_1_out[1]), .Q(OUTPUT[1]), .en(ENABLER));  // open: Qn, preset, reset
  D_Flip_Flop d_ff_3 (
    .clk(CLOCK_SIGNAL), .D(multiplexer_1_out[2]), .Q(OUTPUT[2]), .en(ENABLER));  // open: Qn, preset, reset
  D_Flip_Flop d_ff_4 (
    .clk(CLOCK_SIGNAL), .D(multiplexer_1_out[3]), .Q(OUTPUT[3]), .en(ENABLER));  // open: Qn, preset, reset
  D_Flip_Flop d_ff_5 (
    .clk(CLOCK_SIGNAL), .D(multiplexer_1_out[4]), .Q(OUTPUT[4]), .en(ENABLER));  // open: Qn, preset, reset
  D_Flip_Flop d_ff_6 (
    .clk(CLOCK_SIGNAL), .D(multiplexer_1_out[5]), .Q(OUTPUT[5]), .en(ENABLER));  // open: Qn, preset, reset
  D_Flip_Flop d_ff_7 (
    .clk(CLOCK_SIGNAL), .D(multiplexer_1_out[6]), .Q(OUTPUT[6]), .en(ENABLER));  // open: Qn, preset, reset
  D_Flip_Flop d_ff_8 (
    .clk(CLOCK_SIGNAL), .D(multiplexer_1_out[7]), .Q(OUTPUT[7]), .en(ENABLER));  // open: Qn, preset, reset

  // Notes on the sheet:
  //   INPUT DISPLAY
  //   OUTPUT DISPLAY
  //   clear
endmodule

module _16bit_register (
  input  CLOCK_SIGNAL,
  input  [15:0] INPUT,
  input  [1:0] FunSel,
  input  ENABLER,
  output [15:0] OUTPUT
);

  wire [15:0] adder_1_out, bit_extender_1_out, multiplexer_1_out, xor_1_out;

  Hex_Digit_Display hex_digit_display_1 (.value(INPUT[15:12]));  // open: dp
  Hex_Digit_Display hex_digit_display_2 (.value(OUTPUT[15:12]));  // open: dp
  Hex_Digit_Display hex_digit_display_3 (.value(INPUT[11:8]));  // open: dp
  Hex_Digit_Display hex_digit_display_4 (.value(INPUT[7:4]));  // open: dp
  Hex_Digit_Display hex_digit_display_5 (.value(OUTPUT[11:8]));  // open: dp
  Hex_Digit_Display hex_digit_display_6 (.value(INPUT[3:0]));  // open: dp
  Hex_Digit_Display hex_digit_display_7 (.value(OUTPUT[3:0]));  // open: dp
  Hex_Digit_Display hex_digit_display_8 (.value(OUTPUT[7:4]));  // open: dp
  assign bit_extender_1_out = {{15{FunSel[0]}}, FunSel[0]};  // Bit_Extender bit_extender_1
  assign xor_1_out = 16'h1 ^ bit_extender_1_out;  // XOR_Gate xor_1, 16 bits wide
  Adder #(.width(16)) adder_1 (.a(xor_1_out), .b(OUTPUT), .out(adder_1_out), .cin(FunSel[0]));  // open: cout
  Multiplexer #(.select(2), .width(16), .enable("false")) multiplexer_1 (
    .in0({16{1'b0}}), .in1(INPUT), .in2(adder_1_out), .in3(adder_1_out), .out(multiplexer_1_out), .sel(FunSel));
  D_Flip_Flop d_ff_1 (
    .clk(CLOCK_SIGNAL), .D(multiplexer_1_out[0]), .Q(OUTPUT[0]), .en(ENABLER));  // open: Qn, preset, reset
  D_Flip_Flop d_ff_2 (
    .clk(CLOCK_SIGNAL), .D(multiplexer_1_out[1]), .Q(OUTPUT[1]), .en(ENABLER));  // open: Qn, preset, reset
  D_Flip_Flop d_ff_3 (
    .clk(CLOCK_SIGNAL), .D(multiplexer_1_out[2]), .Q(OUTPUT[2]), .en(ENABLER));  // open: Qn, preset, reset
  D_Flip_Flop d_ff_4 (
    .clk(CLOCK_SIGNAL), .D(multiplexer_1_out[3]), .Q(OUTPUT[3]), .en(ENABLER));  // open: Qn, preset, reset
  D_Flip_Flop d_ff_5 (
    .clk(CLOCK_SIGNAL), .D(multiplexer_1_out[4]), .Q(OUTPUT[4]), .en(ENABLER));  // open: Qn, preset, reset
  D_Flip_Flop d_ff_6 (
    .clk(CLOCK_SIGNAL), .D(multiplexer_1_out[5]), .Q(OUTPUT[5]), .en(ENABLER));  // open: Qn, preset, reset
  D_Flip_Flop d_ff_7 (
    .clk(CLOCK_SIGNAL), .D(multiplexer_1_out[6]), .Q(OUTPUT[6]), .en(ENABLER));  // open: Qn, preset, reset
  D_Flip_Flop d_ff_8 (
    .clk(CLOCK_SIGNAL), .D(multiplexer_1_out[7]), .Q(OUTPUT[7]), .en(ENABLER));  // open: Qn, preset, reset
  D_Flip_Flop d_ff_9 (
    .clk(CLOCK_SIGNAL), .D(multiplexer_1_out[8]), .Q(OUTPUT[8]), .en(ENABLER));  // open: Qn, preset, reset
  D_Flip_Flop d_ff_10 (
    .clk(CLOCK_SIGNAL), .D(multiplexer_1_out[9]), .Q(OUTPUT[9]), .en(ENABLER));  // open: Qn, preset, reset
  D_Flip_Flop d_ff_11 (
    .clk(CLOCK_SIGNAL), .D(multiplexer_1_out[10]), .Q(OUTPUT[10]), .en(ENABLER));  // open: Qn, preset, reset
  D_Flip_Flop d_ff_12 (
    .clk(CLOCK_SIGNAL), .D(multiplexer_1_out[11]), .Q(OUTPUT[11]), .en(ENABLER));  // open: Qn, preset, reset
  D_Flip_Flop d_ff_13 (
    .clk(CLOCK_SIGNAL), .D(multiplexer_1_out[12]), .Q(OUTPUT[12]), .en(ENABLER));  // open: Qn, preset, reset
  D_Flip_Flop d_ff_14 (
    .clk(CLOCK_SIGNAL), .D(multiplexer_1_out[13]), .Q(OUTPUT[13]), .en(ENABLER));  // open: Qn, preset, reset
  D_Flip_Flop d_ff_15 (
    .clk(CLOCK_SIGNAL), .D(multiplexer_1_out[14]), .Q(OUTPUT[14]), .en(ENABLER));  // open: Qn, preset, reset
  D_Flip_Flop d_ff_16 (
    .clk(CLOCK_SIGNAL), .D(multiplexer_1_out[15]), .Q(OUTPUT[15]), .en(ENABLER));  // open: Qn, preset, reset

  // Notes on the sheet:
  //   INPUT DISPLAY
  //   OUTPUT DISPLAY
  //   clear
endmodule

module part2a (
  input  CLOCK,
  input  [7:0] INPUT,
  input  [1:0] FUNSEL,
  input  [3:0] REGSEL,
  input  [1:0] OutASel,
  input  [1:0] OutBSel,
  output [7:0] OutA,
  output [7:0] OutB
);

  wire [7:0] n8bit_register_1_output, n8bit_register_2_output, n8bit_register_3_output,
       n8bit_register_4_output;

  Hex_Digit_Display hex_digit_display_1 (.value(INPUT[7:4]));  // open: dp
  Hex_Digit_Display hex_digit_display_2 (.value(INPUT[3:0]));  // open: dp
  _8bit_register u_8bit_register_1 (
    .CLOCK_SIGNAL(CLOCK), .INPUT(INPUT), .FunSel(FUNSEL), .OUTPUT(n8bit_register_1_output),
    .ENABLER(REGSEL[0]));
  _8bit_register u_8bit_register_2 (
    .CLOCK_SIGNAL(CLOCK), .INPUT(INPUT), .FunSel(FUNSEL), .OUTPUT(n8bit_register_2_output),
    .ENABLER(REGSEL[1]));
  _8bit_register u_8bit_register_3 (
    .CLOCK_SIGNAL(CLOCK), .INPUT(INPUT), .FunSel(FUNSEL), .OUTPUT(n8bit_register_3_output),
    .ENABLER(REGSEL[2]));
  _8bit_register u_8bit_register_4 (
    .CLOCK_SIGNAL(CLOCK), .INPUT(INPUT), .FunSel(FUNSEL), .OUTPUT(n8bit_register_4_output),
    .ENABLER(REGSEL[3]));
  Multiplexer #(.select(2), .width(8), .enable("false")) multiplexer_1 (
    .in0(n8bit_register_1_output), .in1(n8bit_register_2_output), .in2(n8bit_register_3_output),
    .in3(n8bit_register_4_output), .out(OutA), .sel(OutASel));
  Multiplexer #(.select(2), .width(8), .enable("false")) multiplexer_2 (
    .in0(n8bit_register_1_output), .in1(n8bit_register_2_output), .in2(n8bit_register_3_output),
    .in3(n8bit_register_4_output), .out(OutB), .sel(OutBSel));
  Hex_Digit_Display hex_digit_display_3 (.value(OutA[7:4]));  // open: dp
  Hex_Digit_Display hex_digit_display_4 (.value(OutB[7:4]));  // open: dp
  Hex_Digit_Display hex_digit_display_5 (.value(OutA[3:0]));  // open: dp
  Hex_Digit_Display hex_digit_display_6 (.value(OutB[3:0]));  // open: dp

  // Notes on the sheet:
  //   INPUT DISPLAY
  //   OUTPUT A DISPLAY
  //   OUTPUT B DISPLAY
endmodule

module part2b (
  input  CLOCK,
  input  [7:0] INPUT,
  input  [1:0] FunSel,
  input  [2:0] RegSel,
  input  [1:0] OutCSel,
  input  [1:0] OutDSel,
  output [7:0] OUTPUT_C,
  output [7:0] OUTPUT_D
);

  wire [7:0] AR_output, PC_output, SP_output;

  Hex_Digit_Display hex_digit_display_1 (.value(INPUT[3:0]));  // open: dp
  Hex_Digit_Display hex_digit_display_2 (.value(INPUT[7:4]));  // open: dp
  _8bit_register PC (.CLOCK_SIGNAL(CLOCK), .INPUT(INPUT), .FunSel(FunSel), .OUTPUT(PC_output), .ENABLER(RegSel[0]));
  _8bit_register AR (.CLOCK_SIGNAL(CLOCK), .INPUT(INPUT), .FunSel(FunSel), .OUTPUT(AR_output), .ENABLER(RegSel[1]));
  _8bit_register SP (.CLOCK_SIGNAL(CLOCK), .INPUT(INPUT), .FunSel(FunSel), .OUTPUT(SP_output), .ENABLER(RegSel[2]));
  Hex_Digit_Display hex_digit_display_3 (.value(OUTPUT_C[7:4]));  // open: dp
  Multiplexer #(.select(2), .width(8), .enable("false")) multiplexer_1 (
    .in0(PC_output), .in1(AR_output), .in2(SP_output), .in3(PC_output), .out(OUTPUT_C), .sel(OutCSel));
  Multiplexer #(.select(2), .width(8), .enable("false")) multiplexer_2 (
    .in0(PC_output), .in1(AR_output), .in2(SP_output), .in3(PC_output), .out(OUTPUT_D), .sel(OutDSel));
  Hex_Digit_Display hex_digit_display_4 (.value(OUTPUT_C[3:0]));  // open: dp
  Hex_Digit_Display hex_digit_display_5 (.value(OUTPUT_D[7:4]));  // open: dp
  Hex_Digit_Display hex_digit_display_6 (.value(OUTPUT_D[3:0]));  // open: dp

  // Notes on the sheet:
  //   INPUT DISPLAY
  //   OUTPUT C DISPLAY
  //   OUTPUT D DISPLAY
endmodule

module part2c (
  input  CLOCK,
  input  [7:0] INPUT,
  input  L_H_SIGNAL,
  input  [1:0] FunSel,
  input  ENABLE,
  output [7:0] Out_High,
  output [7:0] Out_Low
);

  wire [15:0] adder_1_out, bit_extender_1_out, multiplexer_1_out, multiplexer_2_out, xor_1_out;

  Hex_Digit_Display hex_digit_display_1 (.value(Out_High[7:4]));  // open: dp
  Hex_Digit_Display hex_digit_display_2 (.value(INPUT[7:4]));  // open: dp
  Hex_Digit_Display hex_digit_display_3 (.value(Out_Low[7:4]));  // open: dp
  Hex_Digit_Display hex_digit_display_4 (.value(Out_High[3:0]));  // open: dp
  Hex_Digit_Display hex_digit_display_5 (.value(INPUT[3:0]));  // open: dp
  Hex_Digit_Display hex_digit_display_6 (.value(Out_Low[3:0]));  // open: dp
  Multiplexer #(.width(16), .enable("false")) multiplexer_1 (
    .in0({Out_High, INPUT}), .in1({INPUT, Out_Low}), .out(multiplexer_1_out), .sel(L_H_SIGNAL));
  assign xor_1_out = 16'h1 ^ bit_extender_1_out;  // XOR_Gate xor_1, 16 bits wide
  assign bit_extender_1_out = {{15{FunSel[1]}}, FunSel[1]};  // Bit_Extender bit_extender_1
  Adder #(.width(16)) adder_1 (
    .a(xor_1_out), .b({Out_High, Out_Low}), .out(adder_1_out), .cin(FunSel[1]));  // open: cout
  Multiplexer #(.select(2), .width(16), .enable("false")) multiplexer_2 (
    .in0({16{1'b0}}), .in1(adder_1_out), .in2(adder_1_out), .in3(multiplexer_1_out), .out(multiplexer_2_out),
    .sel(FunSel));
  D_Flip_Flop d_ff_1 (.clk(CLOCK), .D(multiplexer_2_out[0]), .Q(Out_Low[0]), .en(ENABLE));  // open: Qn, preset, reset
  D_Flip_Flop d_ff_2 (.clk(CLOCK), .D(multiplexer_2_out[1]), .Q(Out_Low[1]), .en(ENABLE));  // open: Qn, preset, reset
  D_Flip_Flop d_ff_3 (.clk(CLOCK), .D(multiplexer_2_out[2]), .Q(Out_Low[2]), .en(ENABLE));  // open: Qn, preset, reset
  D_Flip_Flop d_ff_4 (.clk(CLOCK), .D(multiplexer_2_out[3]), .Q(Out_Low[3]), .en(ENABLE));  // open: Qn, preset, reset
  D_Flip_Flop d_ff_5 (.clk(CLOCK), .D(multiplexer_2_out[4]), .Q(Out_Low[4]), .en(ENABLE));  // open: Qn, preset, reset
  D_Flip_Flop d_ff_6 (.clk(CLOCK), .D(multiplexer_2_out[5]), .Q(Out_Low[5]), .en(ENABLE));  // open: Qn, preset, reset
  D_Flip_Flop d_ff_7 (.clk(CLOCK), .D(multiplexer_2_out[6]), .Q(Out_Low[6]), .en(ENABLE));  // open: Qn, preset, reset
  D_Flip_Flop d_ff_8 (.clk(CLOCK), .D(multiplexer_2_out[7]), .Q(Out_Low[7]), .en(ENABLE));  // open: Qn, preset, reset
  D_Flip_Flop d_ff_9 (.clk(CLOCK), .D(multiplexer_2_out[8]), .Q(Out_High[0]), .en(ENABLE));  // open: Qn, preset, reset
  D_Flip_Flop d_ff_10 (.clk(CLOCK), .D(multiplexer_2_out[9]), .Q(Out_High[1]), .en(ENABLE));  // open: Qn, preset, reset
  D_Flip_Flop d_ff_11 (
    .clk(CLOCK), .D(multiplexer_2_out[10]), .Q(Out_High[2]), .en(ENABLE));  // open: Qn, preset, reset
  D_Flip_Flop d_ff_12 (
    .clk(CLOCK), .D(multiplexer_2_out[11]), .Q(Out_High[3]), .en(ENABLE));  // open: Qn, preset, reset
  D_Flip_Flop d_ff_13 (
    .clk(CLOCK), .D(multiplexer_2_out[12]), .Q(Out_High[4]), .en(ENABLE));  // open: Qn, preset, reset
  D_Flip_Flop d_ff_14 (
    .clk(CLOCK), .D(multiplexer_2_out[13]), .Q(Out_High[5]), .en(ENABLE));  // open: Qn, preset, reset
  D_Flip_Flop d_ff_15 (
    .clk(CLOCK), .D(multiplexer_2_out[14]), .Q(Out_High[6]), .en(ENABLE));  // open: Qn, preset, reset
  D_Flip_Flop d_ff_16 (
    .clk(CLOCK), .D(multiplexer_2_out[15]), .Q(Out_High[7]), .en(ENABLE));  // open: Qn, preset, reset

  // Notes on the sheet:
  //   INPUT DISPLAY
  //   OUTPUT DISPLAY
endmodule

module ALU (
  input  CLOCK,
  input  [7:0] A,
  input  [7:0] B,
  input  [3:0] FUNSEL,
  output [3:0] ZCNO,
  output [7:0] OutFLAG
);

  wire adder_1_cout, adder_2_cout, and_1_out, and_3_out, multiplexer_1_out, multiplexer_3_out,
       multiplexer_5_out, nor_1_out, not_3_out, or_1_out, xor_2_out, xor_3_out, xor_5_out;
  wire [0:0] multiplexer_2_out;
  wire [6:0] adder_1_out;
  wire [7:0] and_2_out, bit_extender_1_out, not_1_out, not_2_out, or_2_out, xor_1_out, xor_4_out;
  wire [7:7] adder_2_out, multiplexer_4_out;

  Multiplexer #(.select(4), .enable("false")) multiplexer_1 (
    .in0(ZCNO[0]), .in1(ZCNO[0]), .in2(ZCNO[0]), .in3(ZCNO[0]), .in4(xor_3_out), .in5(xor_3_out),
    .in6(xor_3_out), .in7(ZCNO[0]), .in8(ZCNO[0]), .in9(ZCNO[0]), .in10(ZCNO[0]), .in11(ZCNO[0]),
    .in12(xor_2_out), .in13(ZCNO[0]), .in14(xor_2_out), .in15(xor_5_out), .out(multiplexer_1_out),
    .sel(FUNSEL));
  assign bit_extender_1_out = {{7{FUNSEL[1]}}, FUNSEL[1]};  // Bit_Extender bit_extender_1
  D_Flip_Flop O (.clk(CLOCK), .D(multiplexer_1_out), .Q(ZCNO[0]));  // open: Qn, preset, en, reset
  assign xor_1_out = B ^ bit_extender_1_out;  // XOR_Gate xor_1, 8 bits wide
  assign not_1_out = ~A;  // NOT_Gate not_1, 8 bits wide
  assign not_2_out = ~B;  // NOT_Gate not_2, 8 bits wide
  Multiplexer #(.select(2), .enable("false")) multiplexer_2 (
    .in1(1'b0), .in2(1'b0), .in3(ZCNO[2]), .out(multiplexer_2_out[0]), .sel(FUNSEL[2:1]));  // open: in0
  and and_1 (and_1_out, ZCNO[2], FUNSEL[0]);
  xor xor_2 (xor_2_out, A[7], A[6]);
  Hex_Digit_Display hex_digit_display_1 (.value(A[7:4]));  // open: dp
  Multiplexer #(.select(4), .enable("false")) multiplexer_3 (
    .in0(ZCNO[2]), .in1(ZCNO[2]), .in2(ZCNO[2]), .in3(ZCNO[2]), .in4(adder_2_cout), .in5(adder_2_cout),
    .in6(adder_2_cout), .in7(ZCNO[2]), .in8(ZCNO[2]), .in9(ZCNO[2]), .in10(A[7]), .in11(A[0]),
    .in12(ZCNO[2]), .in13(ZCNO[2]), .in14(A[7]), .in15(A[0]), .out(multiplexer_3_out), .sel(FUNSEL));
  or or_1 (or_1_out, and_1_out, FUNSEL[1]);
  Hex_Digit_Display hex_digit_display_2 (.value(A[3:0]));  // open: dp
  D_Flip_Flop C (.clk(CLOCK), .D(multiplexer_3_out), .Q(ZCNO[2]));  // open: Qn, preset, en, reset
  Adder #(.width(7)) adder_1 (.a(A[6:0]), .b(xor_1_out[6:0]), .out(adder_1_out), .cin(or_1_out), .cout(adder_1_cout));
  Adder #(.width(1)) adder_2 (
    .a(A[7]), .b(xor_1_out[7]), .out(adder_2_out[7]), .cin(adder_1_cout), .cout(adder_2_cout));
  assign and_2_out = A & B;  // AND_Gate and_2, 8 bits wide
  Hex_Digit_Display hex_digit_display_3 (.value(B[7:4]));  // open: dp
  xor xor_3 (xor_3_out, adder_1_cout, adder_2_cout);
  assign or_2_out = A | B;  // OR_Gate or_2, 8 bits wide
  assign xor_4_out = A ^ B;  // XOR_Gate xor_4, 8 bits wide
  Multiplexer #(.select(2), .enable("false")) multiplexer_4 (
    .in0(1'b1), .in1(1'b0), .in2(A[7]), .in3(ZCNO[2]), .out(multiplexer_4_out[7]), .sel(FUNSEL[2:1]));
  Hex_Digit_Display hex_digit_display_4 (.value(B[3:0]));  // open: dp
  nor nor_1 (nor_1_out, OutFLAG[0], OutFLAG[1], OutFLAG[2], OutFLAG[3], OutFLAG[4], OutFLAG[5], OutFLAG[6], OutFLAG[7]);
  D_Flip_Flop Z (.clk(CLOCK), .D(nor_1_out), .Q(ZCNO[3]));  // open: Qn, preset, en, reset
  xor xor_5 (xor_5_out, A[7], multiplexer_4_out[7]);
  Hex_Digit_Display hex_digit_display_5 (.value(FUNSEL));  // open: dp
  Multiplexer #(.enable("false")) multiplexer_5 (
    .in0(OutFLAG[7]), .in1(ZCNO[1]), .out(multiplexer_5_out), .sel(and_3_out));
  and and_3 (and_3_out, FUNSEL[0], not_3_out, FUNSEL[2], FUNSEL[3]);
  D_Flip_Flop N (.clk(CLOCK), .D(multiplexer_5_out), .Q(ZCNO[1]));  // open: Qn, preset, en, reset
  not not_3 (not_3_out, FUNSEL[1]);
  Multiplexer #(.select(4), .width(8), .enable("false")) multiplexer_6 (
    .in0(A), .in1(B), .in2(not_1_out), .in3(not_2_out), .in4({adder_2_out[7], adder_1_out}),
    .in5({adder_2_out[7], adder_1_out}), .in6({adder_2_out[7], adder_1_out}), .in7(and_2_out),
    .in8(or_2_out), .in9(xor_4_out), .in10({A[6:0], multiplexer_2_out[0]}),
    .in11({multiplexer_4_out[7], A[7:1]}), .in12({A[6:0], multiplexer_2_out[0]}),
    .in13({multiplexer_4_out[7], A[7:1]}), .in14({A[6:0], multiplexer_2_out[0]}),
    .in15({multiplexer_4_out[7], A[7:1]}), .out(OutFLAG), .sel(FUNSEL));
  Hex_Digit_Display hex_digit_display_6 (.value(OutFLAG[7:4]));  // open: dp
  Hex_Digit_Display hex_digit_display_7 (.value(ZCNO));  // open: dp
  Hex_Digit_Display hex_digit_display_8 (.value(OutFLAG[3:0]));  // open: dp

  // Notes on the sheet:
  //   A
  //   B
  //   FUNSEL
  //   OutFlag
  //   ZCNO
endmodule

module \new  (
  output [7:0] IR_8_15
);

  wire CLOCK, Enable, L_H, MuxCSEL, store, Z;
  wire [1:0] FunSelA, FunSelC, FunSelIR, MuxASEL, MuxBSEL, OutASel, OutBSel, OutCSel, OutDSel;
  wire [2:0] ALU_zcno, RegSelC;
  wire [3:0] FUNSEL_ALU, multiplexer_2_out, multiplexer_2_out_2, ram_1_data, ram_1_data_2, RegSelA;
  wire [7:0] ALU_outflag, multiplexer_1_out, multiplexer_3_out, OUTLOW, P1_Part2a_outa, P1_Part2a_outb,
       P1_Part2b_output_c, P1_Part2b_output_d;

  Clock clock_1 (.out(CLOCK));
  Hex_Digit_Display hex_digit_display_1 (.value(multiplexer_1_out[7:4]));  // open: dp
  Multiplexer #(.select(2), .width(8), .enable("false")) multiplexer_1 (
    .in0(OUTLOW), .in1({ram_1_data_2, ram_1_data}), .in2(P1_Part2b_output_c), .in3(ALU_outflag),
    .out(multiplexer_1_out), .sel(MuxASEL));
  Hex_Digit_Display hex_digit_display_2 (.value(OUTLOW[3:0]));  // open: dp
  Hex_Digit_Display hex_digit_display_3 (.value(OUTLOW[7:4]));  // open: dp
  part2a P1_Part2a (
    .CLOCK(CLOCK), .OutA(P1_Part2a_outa), .INPUT(multiplexer_1_out), .FUNSEL(FunSelA), .OutB(P1_Part2a_outb),
    .REGSEL(RegSelA), .OutASel(OutASel), .OutBSel(OutBSel));
  Hex_Digit_Display hex_digit_display_4 (.value(multiplexer_1_out[3:0]));  // open: dp
  part2c part2c_1 (
    .Out_High(IR_8_15), .CLOCK(CLOCK), .Out_Low(OUTLOW), .INPUT({ram_1_data_2, ram_1_data}),
    .L_H_SIGNAL(L_H), .FunSel(FunSelIR), .ENABLE(Enable));
  Multiplexer #(.width(8), .enable("false")) multiplexer_2 (
    .in0(multiplexer_1_out), .in1(P1_Part2a_outa), .out({multiplexer_2_out_2, multiplexer_2_out}),
    .sel(MuxCSEL));
  Multiplexer #(.select(2), .width(8), .enable("false")) multiplexer_3 (
    .in0(OUTLOW), .in1(OUTLOW), .in2({ram_1_data_2, ram_1_data}), .in3(ALU_outflag), .out(multiplexer_3_out),
    .sel(MuxBSEL));
  Hex_Digit_Display hex_digit_display_5 (.value(multiplexer_2_out_2));  // open: dp
  Hex_Digit_Display hex_digit_display_6 (.value(multiplexer_2_out));  // open: dp
  part2b P1_Part2b (
    .CLOCK(CLOCK), .INPUT(multiplexer_3_out), .FunSel(FunSelC), .RegSel(RegSelC), .OutCSel(OutCSel),
    .OutDSel(OutDSel), .OUTPUT_C(P1_Part2b_output_c), .OUTPUT_D(P1_Part2b_output_d));
  Hex_Digit_Display hex_digit_display_7 (.value({Z, ALU_zcno}));  // open: dp
  ALU ALU (
    .CLOCK(CLOCK), .A({multiplexer_2_out_2, multiplexer_2_out}), .B(P1_Part2a_outb), .FUNSEL(FUNSEL_ALU),
    .ZCNO({Z, ALU_zcno}), .OutFLAG(ALU_outflag));
  Hex_Digit_Display hex_digit_display_8 (.value(ALU_outflag[7:4]));  // open: dp
  Hex_Digit_Display hex_digit_display_9 (.value(P1_Part2b_output_d[3:0]));  // open: dp
  Hex_Digit_Display hex_digit_display_10 (.value(P1_Part2b_output_d[7:4]));  // open: dp
  Hex_Digit_Display hex_digit_display_11 (.value(IR_8_15[7:4]));  // open: dp
  Hex_Digit_Display hex_digit_display_12 (.value(ALU_outflag[3:0]));  // open: dp
  Hex_Digit_Display hex_digit_display_13 (.value(IR_8_15[3:0]));  // open: dp
  Hex_Digit_Display hex_digit_display_14 (.value(ram_1_data_2));  // open: dp
  Hex_Digit_Display hex_digit_display_15 (.value(ram_1_data));  // open: dp
  RAM #(.bus("separate")) ram_1 (
    .addr(P1_Part2b_output_d), .din(ALU_outflag), .data({ram_1_data_2, ram_1_data}), .str(store),
    .clk(CLOCK), .ld(1'b1));  // open: sel, clr
  control_circuit control_circuit_1 (
    .IR({IR_8_15, OUTLOW}), .Z(Z), .CLOCK(CLOCK), .FunSelIR(FunSelIR), .OutASel(OutASel), .FunSelA(FunSelA),
    .RegSelA(RegSelA), .OutBSel(OutBSel), .MuxASEL(MuxASEL), .MuxBSel(MuxBSEL), .MuxCSEL(MuxCSEL),
    .FUNSEL_ALU(FUNSEL_ALU), .Enable(Enable), .L_H(L_H), .RegSelC(RegSelC), .OutDSel(OutDSel),
    .FunSelC(FunSelC), .OutCSel(OutCSel), .store(store));

  // Other names for the same wires on the sheet: OUTHIGH[7:0] = IR_8_15

  // Notes on the sheet:
  //   OUTPUT DISPLAY
  //   MUX A
  //   OUTPUT DISPLAY
  //   MUX C
  //   MUX B
  //   ALU INPUT A
  //   ZCNO
  //   OUTPUT DISPLAY
  //   OUTPUT ALU
  //   OUTPUT DISPLAY
endmodule

module control_circuit (
  input  [15:0] IR,
  input  CLOCK,
  input  Z,
  output [1:0] FunSelIR,
  output [1:0] OutASel,
  output [1:0] FunSelA,
  output [3:0] RegSelA,
  output [1:0] OutBSel,
  output [1:0] MuxASEL,
  output [1:0] MuxBSel,
  output MuxCSEL,
  output [3:0] FUNSEL_ALU,
  output Enable,
  output L_H,
  output [2:0] RegSelC,
  output [1:0] OutDSel,
  output [1:0] FunSelC,
  output [1:0] OutCSel,
  output store
);

  wire and_1_out, and_2_out, and_3_out, and_4_out, and_5_out, and_6_out, and_7_out, and_8_out, and_9_out,
       and_10_out, and_11_out, and_12_out, and_13_out, and_14_out, and_15_out, and_16_out, and_17_out,
       and_18_out, and_19_out, and_20_out, and_21_out, and_22_out, and_23_out, and_24_out, and_25_out,
       and_26_out, and_27_out, and_28_out, and_29_out, and_30_out, and_31_out, and_32_out, and_33_out,
       and_34_out, and_35_out, and_36_out, and_37_out, and_38_out, and_39_out, and_40_out, and_41_out,
       and_42_out, and_43_out, and_44_out, and_45_out, and_46_out, and_47_out, and_48_out, and_49_out,
       and_50_out, and_51_out, and_52_out, and_54_out, and_55_out, and_56_out, and_57_out, and_58_out,
       and_59_out, and_60_out, and_61_out, and_62_out, and_63_out, and_64_out, and_65_out, and_66_out,
       and_67_out, and_68_out, and_69_out, and_70_out, and_71_out, and_72_out, and_73_out, and_74_out,
       and_76_out, and_77_out, and_78_out, and_79_out, and_80_out, and_81_out, and_82_out, and_83_out,
       and_84_out, and_85_out, and_86_out, and_87_out, and_88_out, and_89_out, and_90_out, and_91_out,
       and_92_out, and_93_out, and_94_out, and_95_out, and_96_out, and_97_out, and_98_out, and_99_out,
       and_100_out, and_101_out, and_102_out, and_103_out, and_104_out, and_105_out, and_106_out,
       and_107_out, and_108_out, and_109_out, and_110_out, and_111_out, and_112_out, and_113_out,
       and_114_out, and_115_out, and_116_out, and_117_out, and_118_out, and_120_out, and_121_out,
       and_122_out, and_123_out, and_124_out, and_125_out, and_126_out, and_127_out, and_128_out,
       and_129_out, and_130_out, and_131_out, and_132_out, and_133_out, and_134_out, and_135_out,
       and_136_out, and_137_out, and_138_out, and_139_out, and_140_out, and_141_out, and_142_out, AR_DEST,
       AR_REG1, AR_REG2, BRANCH, D, D0, D1, D2, D3, D4, D5, D6, D7, D8, D9, D10, D11, D12, D13, D14, D15,
       D16, D17, D18, D_5___13, D_5___13_6, D_5___13_BINARY, D_7___8, D_7___8_t, decoder_1_out5,
       decoder_3_out4, decoder_3_out5, decoder_4_out4, decoder_4_out5, decoder_5_out4, decoder_5_out5,
       DEST_A, DEST_B, IM, not_1_out, not_2_out, not_3_out, or_1_out, or_2_out, or_3_out, or_4_out, or_5_out,
       or_6_out, or_7_out, or_8_out, or_9_out, or_10_out, or_11_out, or_12_out, or_13_out, or_14_out,
       or_15_out, or_18_out, or_21_out, or_22_out, or_24_out, or_25_out, or_29_out, or_31_out, or_33_out,
       or_34_out, or_38_out, or_39_out, or_40_out, or_41_out, or_42_out, or_43_out, or_44_out, or_45_out,
       or_46_out, or_47_out, or_48_out, or_49_out, or_50_out, or_51_out, or_52_out, or_53_out, or_54_out,
       or_55_out, or_56_out, or_57_out, or_58_out, or_59_out, or_60_out, or_61_out, or_62_out, or_63_out,
       or_64_out, PC_DEST, PC_REG1, PC_REG2, R0, R0_DEST, R0_REG1, R0_REG2, R1, R1_DEST, R1_REG1, R1_REG2,
       R2, R2_DEST, R2_REG1, R2_REG2, R3, R3_DEST, R3_REG1, R3_REG2, REG1_A, REG1_B, REG2_A, REG2_B, SP_DEST,
       SP_REG1, SP_REG2, SPE_CON, SPE_CON2, T0, T1, T2, T3, T4;
  wire [2:0] counter_1_q;

  and and_1 (and_1_out, SPE_CON2, R2_DEST);
  Counter #(.width(3), .max('h7)) counter_1 (
    .count(1'b1), .Q(counter_1_q), .clk(CLOCK), .clr(decoder_1_out5));  // open: load, D, carry
  Decoder #(.select(3), .enable("false")) decoder_1 (
    .out0(T0), .out1(T1), .out2(T2), .out3(T3), .out4(T4), .out5(decoder_1_out5), .sel(counter_1_q));  // open: out6, out7
  or or_1 (or_1_out, D2, D_7___8, SPE_CON);
  and and_2 (and_2_out, or_1_out, T2, R2_DEST);
  or or_2 (or_2_out, D7, D8);
  and and_3 (and_3_out, D0, T2, IM, R2);
  and and_4 (and_4_out, D0, T2, D, R3);
  or or_3 (or_3_out, D7, D8);
  and and_5 (and_5_out, or_2_out, AR_DEST, T3);
  or or_4 (or_4_out, D7, D8);
  and and_6 (and_6_out, D0, T2, D, R2);
  and and_7 (and_7_out, D4, T3, R2);
  and and_8 (and_8_out, D0, T2, IM, R3);
  and and_9 (and_9_out, D4, T3, R3);
  and and_10 (and_10_out, or_3_out, PC_DEST, T3);
  and and_11 (and_11_out, D17, IM, T2);
  and and_12 (and_12_out, or_4_out, SP_DEST, T3);
  Decoder #(.select(5), .enable("false")) decoder_2 (
    .out0(D0), .out1(D1), .out2(D2), .out3(D3), .out4(D4), .out5(D5), .out6(D6), .out7(D7), .out8(D8),
    .out9(D9), .out10(D10), .out11(D11), .out12(D12), .out13(D13), .out14(D14), .out15(D15), .out16(D16),
    .out17(D17), .out18(D18), .sel(IR[15:11]));  // open: out19, out20, out21, out22, out23, out24, out25, out26, out27, out28, out29, out30, out31
  or or_5 (or_5_out, and_3_out, and_2_out, and_1_out, and_6_out, and_7_out);
  and and_13 (and_13_out, D18, T3);
  and and_14 (and_14_out, D18, T2);
  and and_15 (and_15_out, D0, T2, D, R1);
  and and_16 (and_16_out, D17, IM, T3);
  and and_17 (and_17_out, D3, T2);
  and and_18 (and_18_out, D4, T2);
  or or_6 (or_6_out, D_5___13, D2);
  Decoder #(.select(3), .enable("false")) decoder_3 (
    .out0(R0_DEST), .out1(R1_DEST), .out2(R2_DEST), .out3(R3_DEST), .out4(decoder_3_out4),
    .out5(decoder_3_out5), .out6(AR_DEST), .out7(SP_DEST), .sel(IR[10:8]));
  and and_19 (and_19_out, D0, T2, IM, R1);
  and and_20 (and_20_out, D4, T3, R1);
  and and_21 (and_21_out, D11, T2);
  and and_22 (and_22_out, D5, T2);
  and and_23 (and_23_out, D6, T2);
  and and_24 (and_24_out, D9, T2);
  or or_7 (or_7_out, D_5___13, D2);
  or or_8 (or_8_out, SPE_CON, D_7___8, D2);
  and and_25 (and_25_out, D0, T2, D, R0);
  and and_26 (and_26_out, D0, T2, IM, R0);
  and and_27 (and_27_out, D10, T2);
  and and_28 (and_28_out, or_7_out, PC_DEST, T2);
  or or_9 (or_9_out, D_5___13, D2);
  and and_29 (and_29_out, or_6_out, SP_DEST, T2);
  and and_30 (and_30_out, or_8_out, T2, R0_DEST);
  and and_31 (and_31_out, D4, T3, R0);
  or or_10 (or_10_out, and_15_out, and_19_out, and_42_out, and_20_out, and_32_out);
  or or_11 (or_11_out, SPE_CON, D_7___8, D2);
  and and_32 (and_32_out, or_11_out, T2, R1_DEST);
  or or_12 (or_12_out, SPE_CON, D_7___8, D2);
  and and_33 (and_33_out, D17, IM, T2);
  or or_13 (or_13_out, and_16_out, BRANCH, T0, T1, and_13_out, and_10_out, and_28_out);
  and and_34 (and_34_out, or_9_out, AR_DEST, T2);
  or or_14 (or_14_out, and_34_out, and_5_out);
  or or_15 (or_15_out, and_17_out, and_18_out, and_11_out, and_14_out, and_29_out, and_12_out);
  or or_16 (PC_DEST, decoder_3_out5, decoder_3_out4);
  or or_17 (D_5___13, D5, D6, D7, D8, D9, D10, D11, D12, D13);
  and and_35 (and_35_out, SPE_CON2, R0_DEST);
  or or_18 (or_18_out, and_30_out, and_25_out, and_35_out, and_26_out, and_31_out);
  and and_36 (and_36_out, or_12_out, T2, R3_DEST);
  and and_37 (and_37_out, D3, T2);
  or or_19 (DEST_A, R0_DEST, R1_DEST, R2_DEST, R3_DEST);
  or or_20 (DEST_B, decoder_3_out4, decoder_3_out5, AR_DEST, SP_DEST);
  and and_38 (and_38_out, D2, T2);
  and and_39 (and_39_out, D1, T2, D);
  and and_40 (and_40_out, D12, T2);
  and and_41 (and_41_out, D13, T2);
  Priority_Encoder priority_encoder_1 (
    .in0(1'b1), .in1(or_13_out), .in2(or_14_out), .in4(or_15_out), .out(RegSelC));  // open: in3, in5, in6, in7, en_in, gs, en_out
  and and_42 (and_42_out, SPE_CON2, R1_DEST);
  and and_43 (and_43_out, SPE_CON2, R3_DEST);
  or or_21 (or_21_out, and_36_out, and_8_out, and_43_out, and_4_out, and_9_out);
  and and_44 (and_44_out, D8, T2);
  Decoder #(.select(3), .enable("false")) decoder_4 (
    .out0(R0_REG1), .out1(R1_REG1), .out2(R2_REG1), .out3(R3_REG1), .out4(decoder_4_out4),
    .out5(decoder_4_out5), .out6(AR_REG1), .out7(SP_REG1), .sel(IR[7:5]));
  Priority_Encoder #(.select(4)) priority_encoder_2 (
    .in0(1'b1), .in1(or_18_out), .in2(or_10_out), .in4(or_5_out), .in8(or_21_out), .out(RegSelA));  // open: in3, in5, in6, in7, in9, in10, in11, in12, in13, in14, in15, gs, en_out, en_in
  and and_45 (and_45_out, D7, T2);
  or or_22 (or_22_out, and_37_out, and_39_out);
  or or_23 (D_5___13_BINARY, D5, D6, D9, D10, D11, D12, D13);
  or or_24 (or_24_out, and_45_out, and_33_out, and_38_out, and_44_out, and_46_out);
  and and_46 (and_46_out, T4, D_7___8);
  or or_25 (or_25_out, D_5___13, D2);
  or or_26 (PC_REG1, decoder_4_out5, decoder_4_out4);
  Priority_Encoder #(.select(4)) priority_encoder_3 (
    .in0(or_24_out), .in1(or_22_out), .in2(and_21_out), .in4(and_22_out), .in6(and_23_out), .in7(and_24_out),
    .in8(and_27_out), .in10(and_40_out), .in11(and_41_out), .out(FUNSEL_ALU));  // open: in3, in5, in9, in12, in13, in14, in15, gs, en_out, en_in
  and and_47 (and_47_out, or_25_out, DEST_B, T2);
  or or_27 (REG1_A, R0_REG1, R1_REG1, R2_REG1, R3_REG1);
  or or_28 (REG1_B, decoder_4_out4, decoder_4_out5, AR_REG1, SP_REG1);
  and and_48 (and_48_out, D18, T3);
  and and_49 (and_49_out, D17, IM, T3);
  and and_50 (and_50_out, D18, T2);
  and and_51 (and_51_out, D17, IM, T2);
  Decoder #(.select(3), .enable("false")) decoder_5 (
    .out0(R0_REG2), .out1(R1_REG2), .out2(R2_REG2), .out3(R3_REG2), .out4(decoder_5_out4),
    .out5(decoder_5_out5), .out6(AR_REG2), .out7(SP_REG2), .sel(IR[4:2]));
  or or_29 (or_29_out, D7, D8);
  and and_52 (and_52_out, D8, DEST_B, T3);
  or or_30 (D_5___13_6, D5, D7, D8, D9, D10, D11, D12, D13);
  and and_53 (SPE_CON2, or_29_out, DEST_A, T3);
  and and_54 (and_54_out, D7, DEST_B, T3);
  or or_31 (or_31_out, and_48_out, and_49_out, BRANCH, and_47_out);
  and and_55 (and_55_out, D4, T2);
  and and_56 (and_56_out, D3, T2);
  or or_32 (PC_REG2, decoder_5_out5, decoder_5_out4);
  or or_33 (or_33_out, and_50_out, T0, and_52_out, T1, and_55_out);
  or or_34 (or_34_out, and_56_out, and_54_out, and_51_out);
  or or_35 (REG2_A, R0_REG2, R1_REG2, R2_REG2, R3_REG2);
  or or_36 (REG2_B, decoder_5_out4, decoder_5_out5, AR_REG2, SP_REG2);
  or or_37 (D_7___8, D7, D8);
  and and_57 (and_57_out, D17, T2, IM);
  and and_58 (and_58_out, T4, D_7___8, DEST_B);
  and and_59 (and_59_out, T4, D_7___8, DEST_A);
  Priority_Encoder #(.select(2)) priority_encoder_4 (
    .in1(or_31_out), .in2(or_33_out), .in3(or_34_out), .out(FunSelC));  // open: in0, gs, en_out, en_in
  Decoder #(.select(2), .enable("false")) decoder_6 (.out0(R0), .out1(R1), .out2(R2), .out3(R3), .sel(IR[10:9]));
  not not_1 (not_1_out, Z);
  and and_60 (and_60_out, D2, T2, DEST_A);
  and and_61 (and_61_out, D4, T3);
  and and_62 (and_62_out, D0, T2, D);
  and and_63 (and_63_out, D0, T2, IM);
  and and_64 (and_64_out, D8, T3);
  and and_65 (and_65_out, D7, T3);
  and and_66 (and_66_out, D6, T2, REG2_B);
  and and_67 (and_67_out, D2, T2, REG1_B);
  and and_68 (and_68_out, D15, Z);
  and and_69 (and_69_out, D16, not_1_out);
  or or_38 (or_38_out, and_74_out, and_60_out, and_61_out, and_62_out, and_63_out, SPE_CON);
  and and_70 (and_70_out, D_5___13_6, T2, REG1_B);
  and and_71 (and_71_out, D_5___13_6, T2, REG1_A);
  and and_72 (and_72_out, D2, T2, REG1_A);
  and and_73 (and_73_out, D6, T2, REG2_A);
  Decoder #(.enable("false")) decoder_7 (.out0(IM), .out1(D), .sel(IR[8]));
  or or_39 (or_39_out, D14, and_68_out, and_69_out);
  and and_74 (and_74_out, D_7___8_t, T2);
  or or_40 (or_40_out, and_70_out, and_66_out, and_57_out, and_67_out, and_58_out);
  or or_41 (or_41_out, and_71_out, and_59_out, and_72_out, and_73_out);
  and and_75 (BRANCH, or_39_out, IM, T2);
  and and_76 (and_76_out, D18, T3);
  Priority_Encoder #(.select(2)) priority_encoder_5 (
    .in1(or_38_out), .in2(and_64_out), .in3(and_65_out), .out(FunSelA));  // open: in0, gs, en_out, en_in
  Priority_Encoder #(.select(1)) priority_encoder_6 (
    .in0(or_40_out), .in1(or_41_out), .out(MuxCSEL));  // open: gs, en_out, en_in
  and and_77 (and_77_out, T2, D17, IM);
  and and_78 (and_78_out, D0, T2, D);
  and and_79 (and_79_out, D1, T2, D);
  or or_42 (or_42_out, T0, T1);
  or or_43 (or_43_out, and_78_out, and_79_out);
  and and_80 (and_80_out, D3, T2);
  and and_81 (and_81_out, D4, T3);
  or or_44 (or_44_out, and_80_out, and_81_out, and_77_out, and_76_out);
  Priority_Encoder #(.select(2)) priority_encoder_7 (
    .in0(or_42_out), .in1(or_43_out), .in2(or_44_out), .out(OutDSel));  // open: in3, gs, en_out, en_in
  and and_82 (and_82_out, D2, T2, R2_REG1);
  and and_83 (and_83_out, R2_DEST, D_7___8, T4);
  and and_84 (and_84_out, R0_DEST, D_7___8, T4);
  and and_85 (and_85_out, D6, T2, R1_REG2);
  and and_86 (and_86_out, D6, T2, R2_REG2);
  and and_87 (and_87_out, R1_DEST, D_7___8, T4);
  and and_88 (and_88_out, D_5___13_6, T2, R2_REG1);
  and and_89 (and_89_out, D2, T2, R1_REG1);
  and and_90 (and_90_out, D0, T2, D);
  and and_91 (and_91_out, PC_DEST, D_7___8, T4);
  and and_92 (and_92_out, AR_DEST, D_7___8, T4);
  and and_93 (and_93_out, AR_REG1, D2, T2);
  and and_94 (and_94_out, D_5___13_6, T2, R1_REG1);
  and and_95 (and_95_out, SP_DEST, D_7___8, T4);
  and and_96 (and_96_out, D2, T2, R3_REG1);
  and and_97 (and_97_out, D4, T3);
  and and_98 (and_98_out, PC_REG2, D6, T2);
  and and_99 (and_99_out, AR_REG2, D6, T2);
  or or_45 (or_45_out, and_88_out, and_82_out, and_86_out, and_83_out);
  and and_100 (and_100_out, R3_DEST, D_7___8, T4);
  or or_46 (or_46_out, REG1_B, REG2_B);
  and and_101 (and_101_out, IM, D17, T2);
  and and_102 (and_102_out, AR_REG1, D_5___13_6, T2);
  and and_103 (and_103_out, D_5___13_6, T2, R3_REG1);
  and and_104 (and_104_out, D6, T2, R3_REG2);
  and and_105 (and_105_out, IM, T2, D17);
  and and_106 (and_106_out, PC_REG1, D_5___13_6, T2);
  and and_107 (and_107_out, SP_REG1, D2, T2);
  and and_108 (and_108_out, PC_REG1, D2, T2);
  or or_47 (or_47_out, and_102_out, and_99_out, and_93_out, and_92_out);
  and and_109 (and_109_out, SP_REG1, D_5___13_6, T2);
  and and_110 (and_110_out, SP_REG2, D6, T2);
  and and_111 (and_111_out, D2, T2, R0_REG1);
  and and_112 (and_112_out, D_5___13_6, T2, R0_REG1);
  and and_113 (and_113_out, D6, T2, R0_REG2);
  or or_48 (or_48_out, and_94_out, and_89_out, and_85_out, and_87_out);
  and and_114 (and_114_out, D2, T2, REG1_B);
  and and_115 (and_115_out, D_5___13, or_46_out, T2);
  or or_49 (or_49_out, and_109_out, and_110_out, and_107_out, and_95_out);
  or or_50 (or_50_out, and_103_out, and_96_out, and_104_out, and_100_out);
  or or_51 (or_51_out, and_90_out, and_97_out);
  and and_116 (and_116_out, D_7___8, T4);
  or or_52 (or_52_out, and_106_out, and_98_out, and_101_out, and_91_out, and_108_out);
  or or_53 (or_53_out, and_112_out, and_111_out, and_113_out, and_84_out);
  or or_54 (or_54_out, and_114_out, and_115_out, and_116_out, and_105_out);
  Priority_Encoder #(.select(2)) priority_encoder_8 (
    .in0(or_53_out), .in1(or_48_out), .in2(or_45_out), .in3(or_50_out), .out(OutASel));  // open: gs, en_out, en_in
  not not_2 (not_2_out, REG1_B);
  not not_3 (not_3_out, REG2_B);
  Priority_Encoder #(.select(2)) priority_encoder_9 (
    .in0(or_52_out), .in1(or_47_out), .in2(or_49_out), .in3(or_52_out), .out(OutCSel));  // open: gs, en_out, en_in
  and and_117 (and_117_out, D0, T2, IM);
  and and_118 (and_118_out, not_2_out, not_3_out);
  Priority_Encoder #(.select(2)) priority_encoder_10 (
    .in0(and_117_out), .in1(or_51_out), .in2(or_54_out), .in3(SPE_CON), .out(MuxASEL));  // open: gs, en_out, en_in
  and and_119 (SPE_CON, D_5___13_BINARY, DEST_A, T2, and_118_out);
  or or_55 (or_55_out, T0, T1);
  Priority_Encoder #(.select(2)) priority_encoder_11 (
    .in3(or_55_out), .out(FunSelIR));  // open: in0, in1, in2, gs, en_out, en_in
  and and_120 (and_120_out, D18, T3);
  and and_121 (and_121_out, D17, T2, IM);
  and and_122 (and_122_out, D_5___13_6, T2, R1_REG2);
  and and_123 (and_123_out, D6, T2, R1_REG1);
  buf or_56 (or_56_out, and_120_out);  // OR_Gate
  and and_124 (and_124_out, T2, D1, R1, D);
  and and_125 (and_125_out, D_5___13_6, T2, R2_REG2);
  and and_126 (and_126_out, D6, T2, R2_REG1);
  and and_127 (and_127_out, T2, D1, R2, D);
  and and_128 (and_128_out, T2, D3, R2);
  and and_129 (and_129_out, D17, IM, T3);
  and and_130 (and_130_out, D1, T2, D);
  and and_131 (and_131_out, D_5___13_6, T2, R0_REG2);
  or or_57 (or_57_out, and_124_out, and_122_out, and_123_out, and_132_out);
  and and_132 (and_132_out, T2, D3, R1);
  and and_133 (and_133_out, D2, DEST_B, T2);
  or or_58 (or_58_out, T0, T1);
  and and_134 (and_134_out, D3, T2);
  or or_59 (or_59_out, and_125_out, and_126_out, and_127_out, and_128_out);
  Priority_Encoder #(.select(1)) priority_encoder_12 (
    .in0(1'b1), .in1(or_60_out), .out(store));  // open: gs, en_out, en_in
  or or_60 (or_60_out, and_130_out, and_121_out, and_134_out);
  and and_135 (and_135_out, T2, D1, R0, D);
  and and_136 (and_136_out, D6, T2, R0_REG1);
  and and_137 (and_137_out, T2, D3, R0);
  and and_138 (and_138_out, T2, D3, R3);
  and and_139 (and_139_out, D_5___13, DEST_B, T2);
  Priority_Encoder #(.select(1)) priority_encoder_13 (
    .in0(1'b1), .in1(or_58_out), .out(Enable));  // open: gs, en_out, en_in
  Priority_Encoder #(.select(1)) priority_encoder_14 (.in0(T1), .in1(T0), .out(L_H));  // open: gs, en_out, en_in
  or or_61 (or_61_out, and_135_out, and_131_out, and_136_out, and_137_out);
  and and_140 (and_140_out, D6, T2, R3_REG1);
  or or_62 (or_62_out, and_133_out, and_139_out);
  and and_141 (and_141_out, D_5___13_6, T2, R3_REG2);
  or or_63 (or_63_out, and_141_out, and_140_out, and_138_out, and_142_out);
  and and_142 (and_142_out, T2, D1, R3, D);
  or or_64 (or_64_out, and_129_out, BRANCH);
  Priority_Encoder #(.select(2)) priority_encoder_15 (
    .in0(or_64_out), .in2(or_56_out), .in3(or_62_out), .out(MuxBSel));  // open: in1, gs, en_out, en_in
  Priority_Encoder #(.select(2)) priority_encoder_16 (
    .in0(or_61_out), .in1(or_57_out), .in2(or_59_out), .in3(or_63_out), .out(OutBSel));  // open: gs, en_out, en_in
endmodule
